// Logisim project 16_bit_computer.circ as structural Verilog: 30 circuits, main circuit main
module main (
  input  FGO,
  input  FGI,
  input  [7:0] in_3,
  input  Cout,
  output HLT
);

  wire clock_1_out, main_control_1_cle, main_control_1_cme, main_control_1_hlt, main_control_1_outr_load,
       not_1_out;
  wire [1:0] main_control_1_ir_bus_ir_load, main_control_1_m_bus_m_load, main_control_1_tr_bus_tr_load;
  wire [2:0] main_control_1_dr_bus_dr_inc_dr_load;
  wire [3:0] controlled_buffer_1_out_2, controlled_buffer_1_out_3,
       main_control_1_ac_bus_ac_clr_ac_inc_ac_load, main_control_1_ar_bus_ar_inc_ar_clr_ar_load,
       main_control_1_pc_bus_pc_clr_pc_inc_pc_load;
  wire [6:0] main_control_1_alu;
  wire [7:0] controlled_buffer_1_out, OUTR_output, register_8bit_1_output;
  wire [11:0] AR_output, PC_output;
  wire [14:0] AC_output;
  wire [15:0] alu_16bit_1_out_14, DR_output, IR_output, ram_1_data, TR_output;
  wire [15:15] AC_output_2;

  main_control main_control_1 (
    .IR(IR_output), .CLK(HLT), .FGO(FGO), .FGI(FGI), .AC({AC_output_2[15], AC_output}), .E(Cout),
    .AC_15(AC_output_2[15]), .DR(DR_output), .CME(main_control_1_cme), .CLE(main_control_1_cle),
    .HLT(main_control_1_hlt), .M_BUS_M_LOAD(main_control_1_m_bus_m_load),
    .AR_BUS_AR_INC_AR_CLR_AR_LOAD(main_control_1_ar_bus_ar_inc_ar_clr_ar_load),
    .PC_BUS_PC_CLR_PC_INC_PC_LOAD(main_control_1_pc_bus_pc_clr_pc_inc_pc_load),
    .DR_BUS_DR_INC_DR_LOAD(main_control_1_dr_bus_dr_inc_dr_load),
    .AC_BUS_AC_CLR_AC_INC_AC_LOAD(main_control_1_ac_bus_ac_clr_ac_inc_ac_load),
    .OUTR_LOAD(main_control_1_outr_load), .TR_BUS_TR_LOAD(main_control_1_tr_bus_tr_load),
    .IR_BUS_IR_LOAD(main_control_1_ir_bus_ir_load), .ALU(main_control_1_alu));  // open: out_21
  not not_1 (not_1_out, main_control_1_hlt);
  Clock clock_1 (.out(clock_1_out));
  and and_1 (HLT, not_1_out, clock_1_out);
  register_8bit register_8bit_1 (.L_NPUT(in_3), .CLK(HLT), .LOAD(1'b1), .OUTPUT(register_8bit_1_output));
  // Probe on register_8bit_1_output
  alu_16bit alu_16bit_1 (
    .AC({AC_output_2[15], AC_output}), .DR(DR_output), .INPR(register_8bit_1_output),
    .AND(main_control_1_alu[0]), .ADD(main_control_1_alu[1]), .CMA(main_control_1_alu[2]),
    .LD_DR(main_control_1_alu[3]), .LD_INPR(main_control_1_alu[4]), .CIR(main_control_1_alu[5]),
    .CIL(main_control_1_alu[6]), .CLA(main_control_1_cle), .CME(main_control_1_cme), .CLOCK(HLT),
    .out_14(alu_16bit_1_out_14), .OUTPUT(Cout));
  // Probe on alu_16bit_1_out_14
  register_12bit AR (
    .L_NPUT({controlled_buffer_1_out_2, controlled_buffer_1_out}),
    .INC(main_control_1_ar_bus_ar_inc_ar_clr_ar_load[2]), .CLK(HLT),
    .LD(main_control_1_ar_bus_ar_inc_ar_clr_ar_load[0]),
    .CLR(main_control_1_ar_bus_ar_inc_ar_clr_ar_load[1]), .OUTPUT(AR_output));
  // Probe on PC_output
  register_12bit PC (
    .L_NPUT({controlled_buffer_1_out_2, controlled_buffer_1_out}),
    .INC(main_control_1_pc_bus_pc_clr_pc_inc_pc_load[1]), .CLK(HLT),
    .LD(main_control_1_pc_bus_pc_clr_pc_inc_pc_load[0]),
    .CLR(main_control_1_pc_bus_pc_clr_pc_inc_pc_load[2]), .OUTPUT(PC_output));
  register_16bit DR (
    .L_NPUT({controlled_buffer_1_out_3, controlled_buffer_1_out_2, controlled_buffer_1_out}), .CLK(HLT),
    .INC(main_control_1_dr_bus_dr_inc_dr_load[1]), .LD(main_control_1_dr_bus_dr_inc_dr_load[0]),
    .OUTPUT(DR_output));  // open: CLR
  register_16bit AC (
    .L_NPUT(alu_16bit_1_out_14), .CLK(HLT), .INC(main_control_1_ac_bus_ac_clr_ac_inc_ac_load[1]),
    .CLR(main_control_1_ac_bus_ac_clr_ac_inc_ac_load[2]),
    .LD(main_control_1_ac_bus_ac_clr_ac_inc_ac_load[0]), .OUTPUT({AC_output_2[15], AC_output}));
  // Probe on IR_output
  register_16bit IR (
    .L_NPUT({controlled_buffer_1_out_3, controlled_buffer_1_out_2, controlled_buffer_1_out}), .CLK(HLT),
    .LD(main_control_1_ir_bus_ir_load[0]), .OUTPUT(IR_output));  // open: INC, CLR
  // Probe on TR_output
  register_16bit TR (
    .L_NPUT({controlled_buffer_1_out_3, controlled_buffer_1_out_2, controlled_buffer_1_out}), .CLK(HLT),
    .LD(main_control_1_tr_bus_tr_load[0]), .OUTPUT(TR_output));  // open: INC, CLR
  register_8bit OUTR (
    .L_NPUT(controlled_buffer_1_out), .CLK(HLT), .LOAD(main_control_1_outr_load), .OUTPUT(OUTR_output));
  RAM #(.addrWidth(12), .dataWidth(16)) ram_1 (.addr(AR_output), .data(ram_1_data), .clk(HLT));  // open: sel, ld, clr
  // Probe on AR_output
  // Probe on DR_output
  // Probe on {AC_output_2[15], AC_output}
  // Probe on OUTR_output
  assign {controlled_buffer_1_out_3, controlled_buffer_1_out_2, controlled_buffer_1_out} = main_control_1_m_bus_m_load[1] ? ram_1_data : 16'bz;  // Controlled_Buffer controlled_buffer_1
  assign {controlled_buffer_1_out_3, controlled_buffer_1_out_2, controlled_buffer_1_out} = main_control_1_ar_bus_ar_inc_ar_clr_ar_load[3] ? {4'b0000, AR_output} : 16'bz;  // Controlled_Buffer controlled_buffer_2
  assign {controlled_buffer_1_out_3, controlled_buffer_1_out_2, controlled_buffer_1_out} = main_control_1_pc_bus_pc_clr_pc_inc_pc_load[3] ? {4'b0000, PC_output} : 16'bz;  // Controlled_Buffer controlled_buffer_3
  assign {controlled_buffer_1_out_3, controlled_buffer_1_out_2, controlled_buffer_1_out} = main_control_1_dr_bus_dr_inc_dr_load[2] ? DR_output : 16'bz;  // Controlled_Buffer controlled_buffer_4
  assign {controlled_buffer_1_out_3, controlled_buffer_1_out_2, controlled_buffer_1_out} = main_control_1_ac_bus_ac_clr_ac_inc_ac_load[3] ? {AC_output_2[15], AC_output} : 16'bz;  // Controlled_Buffer controlled_buffer_5
  assign {controlled_buffer_1_out_3, controlled_buffer_1_out_2, controlled_buffer_1_out} = main_control_1_ir_bus_ir_load[1] ? IR_output : 16'bz;  // Controlled_Buffer controlled_buffer_6
  assign {controlled_buffer_1_out_3, controlled_buffer_1_out_2, controlled_buffer_1_out} = main_control_1_tr_bus_tr_load[1] ? TR_output : 16'bz;  // Controlled_Buffer controlled_buffer_7
endmodule

module main_control (
  input  E,
  input  [15:0] AC,
  input  [15:0] DR,
  input  AC_15,
  input  [15:0] IR,
  input  CLK,
  input  FGO,
  input  FGI,
  output HLT,
  output [1:0] M_BUS_M_LOAD,
  output [3:0] AR_BUS_AR_INC_AR_CLR_AR_LOAD,
  output [3:0] PC_BUS_PC_CLR_PC_INC_PC_LOAD,
  output [2:0] DR_BUS_DR_INC_DR_LOAD,
  output [3:0] AC_BUS_AC_CLR_AC_INC_AC_LOAD,
  output OUTR_LOAD,
  output [1:0] TR_BUS_TR_LOAD,
  output CME,
  output CLE,
  output [1:0] IR_BUS_IR_LOAD,
  output [6:0] ALU,
  output out_21
);

  wire not_1_out, sc_kontrol_1_sc_clear;
  wire [1:0] decoder_2_out0;
  wire [2:0] flag_kontrol_1_out_15;
  wire [3:0] counter_1_output, decoder_1_out7;
  wire [4:0] decoder_2_out2;
  wire [6:3] decoder_1_out3;

  Decoder #(.select(3)) decoder_1 (
    .out0(decoder_1_out7[3]), .out1(decoder_1_out7[2]), .out2(decoder_1_out7[1]), .out3(decoder_1_out3[3]),
    .out4(decoder_1_out3[4]), .out5(decoder_1_out3[5]), .out6(decoder_1_out3[6]), .out7(decoder_1_out7[0]),
    .sel(IR[14:12]));  // open: en
  SC_kontrol sc_kontrol_1 (
    .D0(decoder_1_out7[3]), .D1(decoder_1_out7[2]), .D2(decoder_1_out7[1]), .D3(decoder_1_out3[3]),
    .D4(decoder_1_out3[4]), .D5(decoder_1_out3[5]), .D6(decoder_1_out3[6]), .D7(decoder_1_out7[0]),
    .T2(decoder_2_out2[0]), .T3(decoder_2_out2[1]), .T4(decoder_2_out2[2]), .T5(decoder_2_out2[3]),
    .T6(decoder_2_out2[4]), .R(flag_kontrol_1_out_15[2]), .I(IR[15]), .IR0(IR[0]), .IR1(IR[1]), .IR2(IR[2]),
    .IR3(IR[3]), .IR4(IR[4]), .IR5(IR[5]), .IR6(IR[6]), .IR7(IR[7]), .IR8(IR[8]), .IR9(IR[9]), .IR10(IR[10]),
    .IR11(IR[11]), .SC_CLEAR(sc_kontrol_1_sc_clear));
  counter counter_1 (.CLK(CLK), .SC_CLEAR(sc_kontrol_1_sc_clear), .OUTPUT(counter_1_output));
  not not_1 (not_1_out, IR[15]);
  Decoder #(.select(4)) decoder_2 (
    .out0(decoder_2_out0[0]), .out1(decoder_2_out0[1]), .out2(decoder_2_out2[0]), .out3(decoder_2_out2[1]),
    .out4(decoder_2_out2[2]), .out5(decoder_2_out2[3]), .out6(decoder_2_out2[4]), .sel(counter_1_output));  // open: out7, out8, out9, out10, out11, out12, out13, out14, out15, en
  and and_1 (HLT, IR[0], decoder_1_out7[0], not_1_out, decoder_2_out2[1]);
  FLAG_KONTROL flag_kontrol_1 (
    .FGI(FGI), .FGO(FGO), .D7(decoder_1_out7[0]), .I(IR[15]), .T3(decoder_2_out2[1]), .IR7(IR[7]),
    .IR6(IR[6]), .T0(decoder_2_out0[0]), .T1(decoder_2_out0[1]), .T2(decoder_2_out2[0]), .IR10(IR[10]),
    .IR11(IR[11]), .CLOCK(CLK), .IEN(out_21), .out_15(flag_kontrol_1_out_15[0]),
    .out_16(flag_kontrol_1_out_15[1]), .out_17(flag_kontrol_1_out_15[2]));
  ALU_kontrol alu_kontrol_1 (
    .D0(decoder_1_out7[3]), .D1(decoder_1_out7[2]), .D2(decoder_1_out7[1]), .D7(decoder_1_out7[0]),
    .I(IR[15]), .T3(decoder_2_out2[1]), .T5(decoder_2_out2[3]), .IR6(IR[6]), .IR7(IR[7]), .IR9(IR[9]),
    .IR11(IR[11]), .AND(ALU[0]), .ADD(ALU[1]), .CMA(ALU[2]), .DR_LOAD(ALU[3]), .INPR_LOAD(ALU[4]),
    .CIR(ALU[5]), .CIL(ALU[6]));
  register_kontrol register_kontrol_1 (
    .R(flag_kontrol_1_out_15[2]), .I(IR[15]), .D0(decoder_1_out7[3]), .D1(decoder_1_out7[2]),
    .D2(decoder_1_out7[1]), .D3(decoder_1_out3[3]), .D4(decoder_1_out3[4]), .D5(decoder_1_out3[5]),
    .D6(decoder_1_out3[6]), .D7(decoder_1_out7[0]), .T0(decoder_2_out0[0]), .T1(decoder_2_out0[1]),
    .T2(decoder_2_out2[0]), .T3(decoder_2_out2[1]), .T4(decoder_2_out2[2]), .T5(decoder_2_out2[3]),
    .T6(decoder_2_out2[4]), .IR1(IR[1]), .IR2(IR[2]), .IR3(IR[3]), .IR4(IR[4]), .IR5(IR[5]), .IR6(IR[6]),
    .IR7(IR[7]), .IR8(IR[8]), .IR9(IR[9]), .IR10(IR[10]), .IR11(IR[11]), .FGO(flag_kontrol_1_out_15[1]),
    .FGI(flag_kontrol_1_out_15[0]), .E(E), .AC(AC), .AC_15(AC_15), .in_6(DR), .CME(CME), .CLE(CLE),
    .M_BUS_M_LOAD(M_BUS_M_LOAD), .AR_BUS_AR_INC_AR_CLR_AR_LOAD(AR_BUS_AR_INC_AR_CLR_AR_LOAD),
    .PC_BUS_PC_CLR_PC_INC_PC_LOAD(PC_BUS_PC_CLR_PC_INC_PC_LOAD),
    .DR_BUS_DR_INC_DR_LOAD(DR_BUS_DR_INC_DR_LOAD),
    .AC_BUS_AC_CLR_AC_INC_AC_LOAD(AC_BUS_AC_CLR_AC_INC_AC_LOAD), .OUTR_LOAD(OUTR_LOAD),
    .TR_BUS_TR_LOAD(TR_BUS_TR_LOAD), .IR_BUS_IR_LOAD(IR_BUS_IR_LOAD));

  // Notes on the sheet:
  //   D0..D7
  //   T0..15
endmodule

// REGİSTER KONTROL
module register_kontrol (
  input  FGO,
  input  FGI,
  input  E,
  input  [15:0] AC,
  input  AC_15,
  input  [15:0] in_6,
  input  R,
  input  I,
  input  D0,
  input  D1,
  input  D2,
  input  D3,
  input  D4,
  input  D5,
  input  D6,
  input  D7,
  input  T0,
  input  T1,
  input  T2,
  input  T3,
  input  T4,
  input  T5,
  input  T6,
  input  IR1,
  input  IR2,
  input  IR3,
  input  IR4,
  input  IR5,
  input  IR6,
  input  IR7,
  input  IR8,
  input  IR9,
  input  IR10,
  input  IR11,
  output [1:0] M_BUS_M_LOAD,
  output [3:0] AR_BUS_AR_INC_AR_CLR_AR_LOAD,
  output [3:0] PC_BUS_PC_CLR_PC_INC_PC_LOAD,
  output [2:0] DR_BUS_DR_INC_DR_LOAD,
  output [3:0] AC_BUS_AC_CLR_AC_INC_AC_LOAD,
  output OUTR_LOAD,
  output [1:0] TR_BUS_TR_LOAD,
  output [1:0] IR_BUS_IR_LOAD,
  output CME,
  output CLE
);

  OUTR_kontrol OUTR (.D7(D7), .I(I), .T3(T3), .IR10(IR10), .OUTR_LOAD(OUTR_LOAD));
  TR_kontrol TR (.R(R), .T0(T0), .T1(T1), .TR_LOAD(TR_BUS_TR_LOAD[0]), .TR_BUS(TR_BUS_TR_LOAD[1]));
  IR_kontrol IR (.R(R), .T1(T1), .T2(T2), .IR_LOAD(IR_BUS_IR_LOAD[0]), .IR_BUS(IR_BUS_IR_LOAD[1]));
  e_control e_control_1 (.D7(D7), .I(I), .T3(T3), .B8(IR8), .B10(IR10), .CLE(CLE), .CME(CME));
  AR_kontrol AR (
    .D7(D7), .I(I), .D4(D4), .D5(D5), .R(R), .T0(T0), .T2(T2), .T3(T3), .T4(T4), .T5(T5),
    .AR_LOAD(AR_BUS_AR_INC_AR_CLR_AR_LOAD[0]), .AR_CLEAR(AR_BUS_AR_INC_AR_CLR_AR_LOAD[1]),
    .AR_INC(AR_BUS_AR_INC_AR_CLR_AR_LOAD[2]), .AR_BUS(AR_BUS_AR_INC_AR_CLR_AR_LOAD[3]));
  DR_kontrol DR (
    .D0(D0), .D1(D1), .D2(D2), .D6(D6), .T4(T4), .T5(T5), .T6(T6), .DR_LD(DR_BUS_DR_INC_DR_LOAD[0]),
    .DR_INC(DR_BUS_DR_INC_DR_LOAD[1]), .DR_BUS(DR_BUS_DR_INC_DR_LOAD[2]));
  mem_control M (
    .R(R), .I(I), .D0(D0), .D1(D1), .D2(D2), .D3(D3), .D5(D5), .D6(D6), .D7(D7), .T1(T1), .T3(T3), .T4(T4),
    .T6(T6), .M_LOAD(M_BUS_M_LOAD[0]), .M_BUS(M_BUS_M_LOAD[1]));
  PC_kontrol PC (
    .DR(in_6), .in_21(AC_15), .AC_15(AC_15), .AC(AC), .E(E), .FGI(FGI), .FGO(FGO), .I(I), .in_2(R), .D4(D4),
    .D5(D5), .D6(D6), .D7(D7), .T0(T0), .T1(T1), .T2(T2), .T3(T3), .T4(T4), .T5(T5), .T6(T6), .IR1(IR1),
    .IR2(IR2), .IR3(IR3), .IR4(IR4), .IR8(IR8), .IR9(IR9), .PC_LD(PC_BUS_PC_CLR_PC_INC_PC_LOAD[0]),
    .PC_INC(PC_BUS_PC_CLR_PC_INC_PC_LOAD[1]), .PC_CLR(PC_BUS_PC_CLR_PC_INC_PC_LOAD[2]),
    .PC_BUS(PC_BUS_PC_CLR_PC_INC_PC_LOAD[3]));
  AC_kontrol ac_kontrol_1 (
    .I(I), .D0(D0), .D1(D1), .D2(D2), .D3(D3), .D4(D4), .D7(D7), .T3(T3), .T4(T4), .T5(T5), .IR5(IR5),
    .IR6(IR6), .IR7(IR7), .IR9(IR9), .IR10(IR10), .IR11(IR11), .AC_LOAD(AC_BUS_AC_CLR_AC_INC_AC_LOAD[0]),
    .AC_INC(AC_BUS_AC_CLR_AC_INC_AC_LOAD[1]), .AC_CLR(AC_BUS_AC_CLR_AC_INC_AC_LOAD[2]),
    .AC_BUS(AC_BUS_AC_CLR_AC_INC_AC_LOAD[3]));
endmodule

module FLAG_KONTROL (
  input  D7,
  input  I,
  input  T3,
  input  IR7,
  input  IR6,
  input  T0,
  input  T1,
  input  T2,
  input  IR10,
  input  IR11,
  input  FGI,
  input  FGO,
  input  CLOCK,
  output IEN,
  output out_15,
  output out_16,
  output out_17
);

  IEN_FF ien_ff_1 (.D7(D7), .I(I), .T3(T3), .IR7(IR7), .IR6(IR6), .R(out_17), .T2(T2), .clock(CLOCK), .IEN(IEN));
  FGI_FF fgi_ff_1 (.FGI(FGI), .D7(D7), .I(I), .T3(T3), .IR11(IR11), .CLOCK(CLOCK), .out_7(out_15));
  FGO_FF fgo_ff_1 (.FGO(FGO), .D7(D7), .I(I), .T3(T3), .IR10(IR10), .CLOCK(CLOCK), .out_7(out_16));
  R_kontrol R (
    .IEN(IEN), .FGI(out_15), .FGO(out_16), .in_1(out_17), .T0(T0), .T1(T1), .T2(T2), .clock(CLOCK), .R(out_17));
endmodule

module AR_kontrol (
  input  D7,
  input  I,
  input  D4,
  input  D5,
  input  R,
  input  T0,
  input  T2,
  input  T3,
  input  T4,
  input  T5,
  output AR_LOAD,
  output AR_CLEAR,
  output AR_INC,
  output AR_BUS
);

  wire and_1_out, and_2_out, and_5_out, and_6_out, not_1_out, not_2_out, or_1_out;

  not not_1 (not_1_out, R);
  not not_2 (not_2_out, D7);
  or or_1 (or_1_out, T2, T0);
  and and_1 (and_1_out, or_1_out, not_1_out);
  and and_2 (and_2_out, I, T3, not_2_out);
  and and_3 (AR_CLEAR, R, T0);
  and and_4 (AR_INC, T4, D5);
  and and_5 (and_5_out, T4, D4);
  and and_6 (and_6_out, T5, D5);
  or or_2 (AR_LOAD, and_1_out, and_2_out);
  or or_3 (AR_BUS, and_5_out, and_6_out);
endmodule

module PC_kontrol (
  input  I,
  input  in_2,
  input  D4,
  input  D5,
  input  D6,
  input  D7,
  input  T0,
  input  T1,
  input  T2,
  input  T3,
  input  T4,
  input  T5,
  input  T6,
  input  IR1,
  input  IR2,
  input  IR3,
  input  IR4,
  input  IR8,
  input  IR9,
  input  [15:0] DR,
  input  in_21,
  input  AC_15,
  input  [15:0] AC,
  input  E,
  input  FGI,
  input  FGO,
  output PC_LD,
  output PC_INC,
  output PC_CLR,
  output PC_BUS
);

  wire and_1_out, and_2_out, and_3_out, and_4_out, and_5_out, and_6_out, and_7_out, and_8_out, and_9_out,
       and_10_out, and_11_out, and_12_out, and_13_out, and_14_out, and_15_out, and_17_out, and_18_out,
       and_19_out, and_20_out, and_21_out, and_22_out, and_23_out, and_24_out, and_25_out, not_1_out,
       not_2_out, not_3_out, not_4_out, not_5_out, not_6_out, not_8_out, not_10_out, or_1_out, p_out, r_out;
  wire [15:0] not_7_out, not_9_out;

  not not_1 (not_1_out, in_2);
  not not_2 (not_2_out, I);
  not not_3 (not_3_out, I);
  not not_4 (not_4_out, I);
  not not_5 (not_5_out, I);
  and and_1 (and_1_out, not_1_out, T1);
  and and_2 (and_2_out, in_2, T2);
  and and_3 (and_3_out, T6, D6);
  and and_4 (and_4_out, D7, T3, not_2_out);
  and r (r_out, T3, D7, not_3_out);
  and and_5 (and_5_out, T3, not_4_out, D7);
  and and_6 (and_6_out, D7, T3, not_5_out);
  and and_7 (and_7_out, I, D7, T3);
  and p (p_out, T3, D7, I);
  and and_8 (and_8_out, and_4_out, IR4);
  and and_9 (and_9_out, r_out, IR3);
  and and_10 (and_10_out, and_5_out, IR2);
  and and_11 (and_11_out, and_6_out, IR1);
  and and_12 (and_12_out, and_7_out, IR9);
  and and_13 (and_13_out, p_out, IR8);
  not not_6 (not_6_out, in_2);
  and and_14 (and_14_out, D4, T4);
  and and_15 (and_15_out, T5, D5);
  assign not_7_out = ~DR;  // NOT_Gate not_7, 16 bits wide
  not not_8 (not_8_out, in_21);
  assign not_9_out = ~AC;  // NOT_Gate not_9, 16 bits wide
  not not_10 (not_10_out, E);
  and and_16 (PC_CLR, T1, in_2);
  or or_1 (or_1_out, in_2, not_6_out);
  and and_17 (and_17_out, and_8_out, not_8_out);
  and and_18 (and_18_out, and_9_out, AC_15);
  and and_19 (and_19_out, and_11_out, not_10_out);
  and and_20 (and_20_out, and_12_out, FGI);
  and and_21 (and_21_out, T4, D5);
  or or_2 (PC_LD, and_14_out, and_15_out);
  and and_22 (and_22_out, and_13_out, FGO);
  and and_23 (and_23_out, or_1_out, T0);
  or or_3 (PC_BUS, and_23_out, and_21_out);
  and and_24 (and_24_out, and_3_out, not_7_out[0], not_7_out[1], not_7_out[2], not_7_out[3], not_7_out[4], not_7_out[5], not_7_out[6], not_7_out[7], not_7_out[8], not_7_out[9], not_7_out[10], not_7_out[11], not_7_out[12], not_7_out[13], not_7_out[14], not_7_out[15]);
  and and_25 (and_25_out, and_10_out, not_9_out[0], not_9_out[1], not_9_out[2], not_9_out[3], not_9_out[4], not_9_out[5], not_9_out[6], not_9_out[7], not_9_out[8], not_9_out[9], not_9_out[10], not_9_out[11], not_9_out[12], not_9_out[13], not_9_out[14], not_9_out[15]);
  or or_4 (PC_INC, and_1_out, and_2_out, and_24_out, and_17_out, and_18_out, and_25_out, and_19_out, and_20_out, and_22_out);
endmodule

module mem_control (
  input  R,
  input  I,
  input  D0,
  input  D1,
  input  D2,
  input  D3,
  input  D5,
  input  D6,
  input  D7,
  input  T1,
  input  T3,
  input  T4,
  input  T6,
  output M_LOAD,
  output M_BUS
);

  wire and_1_out, and_2_out, and_3_out, and_4_out, and_5_out, and_6_out, not_1_out, not_2_out, or_1_out,
       or_2_out;

  or or_1 (or_1_out, D3, D5);
  not not_1 (not_1_out, R);
  not not_2 (not_2_out, D7);
  and and_1 (and_1_out, or_1_out, T4);
  and and_2 (and_2_out, not_2_out, I, T3);
  or or_2 (or_2_out, D0, D1, D2, D6);
  and and_3 (and_3_out, R, T1);
  and and_4 (and_4_out, T6, D6);
  and and_5 (and_5_out, not_1_out, T1);
  and and_6 (and_6_out, or_2_out, T4);
  or or_3 (M_LOAD, and_3_out, and_1_out, and_4_out);
  or or_4 (M_BUS, and_5_out, and_2_out, and_6_out);
endmodule

module DR_kontrol (
  input  D0,
  input  D1,
  input  D2,
  input  D6,
  input  T4,
  input  T5,
  input  T6,
  output DR_LD,
  output DR_INC,
  output DR_BUS
);

  wire or_1_out;

  and and_1 (DR_BUS, T6, D6);
  or or_1 (or_1_out, D0, D1, D2, D6);
  and and_2 (DR_LD, T4, or_1_out);
  and and_3 (DR_INC, T5, D6);
endmodule

module OUTR_kontrol (
  input  D7,
  input  I,
  input  T3,
  input  IR10,
  output OUTR_LOAD
);

  wire and_1_out;

  and and_1 (and_1_out, D7, I, T3);
  and and_2 (OUTR_LOAD, and_1_out, IR10);
endmodule

module IR_kontrol (
  input  R,
  input  T1,
  input  T2,
  output IR_LOAD,
  output IR_BUS
);

  wire not_1_out;

  not not_1 (not_1_out, R);
  and and_1 (IR_LOAD, T1, not_1_out);
  and and_2 (IR_BUS, T2, not_1_out);
endmodule

module TR_kontrol (
  input  R,
  input  T0,
  input  T1,
  output TR_LOAD,
  output TR_BUS
);

  and and_1 (TR_LOAD, T0, R);
  and and_2 (TR_BUS, T1, R);
endmodule

module AC_kontrol (
  input  I,
  input  D0,
  input  D1,
  input  D2,
  input  D3,
  input  D4,
  input  D7,
  input  T3,
  input  T4,
  input  T5,
  input  IR5,
  input  IR6,
  input  IR7,
  input  IR9,
  input  IR10,
  input  IR11,
  output AC_LOAD,
  output AC_INC,
  output AC_CLR,
  output AC_BUS
);

  wire and_1_out, and_4_out, and_5_out, and_6_out, not_1_out, not_2_out, not_3_out, or_1_out, or_2_out,
       p_out, r_out;

  or or_1 (or_1_out, D0, D1, D2);
  not not_1 (not_1_out, I);
  not not_2 (not_2_out, I);
  not not_3 (not_3_out, I);
  and and_1 (and_1_out, T5, or_1_out);
  and r (r_out, T3, D7, not_1_out);
  or or_2 (or_2_out, IR9, IR7, IR6);
  and p (p_out, IR11, I, D7, T3);
  and and_2 (AC_INC, IR5, T3, D7, not_2_out);
  and and_3 (AC_CLR, T3, IR11, D7, not_3_out);
  and and_4 (and_4_out, D3, T4);
  and and_5 (and_5_out, D7, I, T3, IR10);
  and and_6 (and_6_out, r_out, or_2_out);
  or or_3 (AC_BUS, and_4_out, and_5_out);
  or or_4 (AC_LOAD, and_1_out, and_6_out, p_out);
endmodule

// SC_CLEAR
module SC_kontrol (
  input  D0,
  input  D1,
  input  D2,
  input  D3,
  input  D4,
  input  D5,
  input  D6,
  input  D7,
  input  T2,
  input  T3,
  input  T4,
  input  T5,
  input  T6,
  input  R,
  input  I,
  input  IR0,
  input  IR1,
  input  IR2,
  input  IR3,
  input  IR4,
  input  IR5,
  input  IR6,
  input  IR7,
  input  IR8,
  input  IR9,
  input  IR10,
  input  IR11,
  output SC_CLEAR
);

  wire and_1_out, and_2_out, and_3_out, and_4_out, and_5_out, and_6_out, and_7_out, and_8_out, and_9_out,
       not_1_out, or_1_out, or_2_out, or_3_out, or_4_out, or_5_out;

  and and_1 (and_1_out, T2, R);
  or or_1 (or_1_out, D3, D4);
  or or_2 (or_2_out, D0, D1, D2, D5);
  or or_3 (or_3_out, IR6, IR7, IR8, IR9, IR10, IR11);
  and and_2 (and_2_out, I, D7);
  not not_1 (not_1_out, I);
  and and_3 (and_3_out, not_1_out, D7);
  or or_4 (or_4_out, IR0, IR1, IR2, IR3, IR4, IR5, IR6, IR7, IR8, IR9, IR10, IR11);
  and and_4 (and_4_out, and_3_out, or_4_out);
  and and_5 (and_5_out, or_3_out, and_2_out);
  and and_6 (and_6_out, T5, or_2_out);
  and and_7 (and_7_out, T4, or_1_out);
  and and_8 (and_8_out, T6, D6);
  or or_5 (or_5_out, and_5_out, and_4_out);
  and and_9 (and_9_out, or_5_out, T3);
  or or_6 (SC_CLEAR, and_9_out, and_8_out);
endmodule

// ALU_KONTROL
module ALU_kontrol (
  input  D0,
  input  D1,
  input  D2,
  input  D7,
  input  I,
  input  T3,
  input  T5,
  input  IR6,
  input  IR7,
  input  IR9,
  input  IR11,
  output AND,
  output ADD,
  output CMA,
  output DR_LOAD,
  output INPR_LOAD,
  output CIR,
  output CIL
);

  wire and_1_out, and_2_out, not_1_out;

  not not_1 (not_1_out, I);
  and and_1 (and_1_out, T3, not_1_out, D7);
  and and_2 (and_2_out, D7, I, T3);
  and and_3 (AND, D0, T5);
  and and_4 (ADD, D1, T5);
  and and_5 (CMA, and_1_out, IR9);
  and and_6 (DR_LOAD, D2, T5);
  and and_7 (INPR_LOAD, and_2_out, IR11);
  and and_8 (CIR, and_1_out, IR7);
  and and_9 (CIL, and_1_out, IR6);
endmodule

module R_kontrol (
  input  in_1,
  input  T0,
  input  T1,
  input  T2,
  input  IEN,
  input  FGI,
  input  FGO,
  input  clock,
  output R
);

  wire and_1_out, and_2_out, not_1_out, not_2_out, not_3_out, or_1_out;

  not not_1 (not_1_out, T2);
  not not_2 (not_2_out, T1);
  not not_3 (not_3_out, T0);
  or or_1 (or_1_out, FGI, FGO);
  and and_1 (and_1_out, in_1, T2);
  and and_2 (and_2_out, not_1_out, or_1_out);
  J_K_Flip_Flop j_k_ff_1 (.J(and_2_out), .clk(clock), .K(and_1_out), .Q(R));  // open: Qn, preset, reset
endmodule

module e_control (
  input  D7,
  input  I,
  input  T3,
  input  B8,
  input  B10,
  output CLE,
  output CME
);

  wire not_1_out, R_out;

  not not_1 (not_1_out, I);
  and R (R_out, D7, not_1_out, T3);
  and and_1 (CLE, R_out, B10);
  and and_2 (CME, R_out, B8);
endmodule

module FGO_FF (
  input  D7,
  input  I,
  input  T3,
  input  IR10,
  input  CLOCK,
  input  FGO,
  output out_7
);

  wire and_1_out, and_2_out, and_3_out, and_4_out, and_5_out, and_6_out, or_1_out, or_2_out;

  and and_1 (and_1_out, ~and_2_out, FGO);  // AND_Gate
  and and_2 (and_2_out, IR10, T3, I, D7);
  and and_3 (and_3_out, and_1_out, 1'b1);
  and and_4 (and_4_out, and_1_out, ~1'b1);  // AND_Gate
  and and_5 (and_5_out, and_2_out, ~1'b1);  // AND_Gate
  and and_6 (and_6_out, and_2_out, 1'b1);
  or or_1 (or_1_out, and_3_out, and_5_out);
  or or_2 (or_2_out, and_4_out, and_6_out);
  J_K_Flip_Flop j_k_ff_1 (.J(or_1_out), .clk(CLOCK), .K(or_2_out), .Q(out_7));  // open: Qn, preset, reset
endmodule

module FGI_FF (
  input  D7,
  input  I,
  input  T3,
  input  IR11,
  input  CLOCK,
  input  FGI,
  output out_7
);

  wire and_1_out, and_2_out, and_3_out, and_4_out, and_5_out, and_6_out, or_1_out, or_2_out;

  and and_1 (and_1_out, ~and_2_out, FGI);  // AND_Gate
  and and_2 (and_2_out, IR11, T3, I, D7);
  and and_3 (and_3_out, and_1_out, 1'b1);
  and and_4 (and_4_out, and_1_out, ~1'b1);  // AND_Gate
  and and_5 (and_5_out, and_2_out, ~1'b1);  // AND_Gate
  and and_6 (and_6_out, and_2_out, 1'b1);
  or or_1 (or_1_out, and_3_out, and_5_out);
  or or_2 (or_2_out, and_4_out, and_6_out);
  J_K_Flip_Flop j_k_ff_1 (.J(or_1_out), .clk(CLOCK), .K(or_2_out), .Q(out_7));  // open: Qn, preset, reset
endmodule

module IEN_FF (
  input  D7,
  input  I,
  input  T3,
  input  IR7,
  input  IR6,
  input  R,
  input  T2,
  input  clock,
  output IEN
);

  wire and_1_out, and_2_out, and_3_out, or_1_out, P_out;

  and P (P_out, D7, I, T3);
  and and_1 (and_1_out, IR7, P_out);
  and and_2 (and_2_out, P_out, IR6);
  or or_1 (or_1_out, and_2_out, and_3_out);
  and and_3 (and_3_out, R, T2);
  J_K_Flip_Flop j_k_ff_1 (.J(and_1_out), .clk(clock), .K(or_1_out), .Q(IEN));  // open: Qn, preset, reset
endmodule

// reg
module register_4bit (
  input  INC,
  input  LD,
  input  [3:0] L_NPUT,
  input  CLR,
  input  CLK,
  output [3:0] OUTPUT,
  output elde
);

  wire and_1_out, and_2_out, and_3_out, and_4_out, and_5_out, and_6_out, and_7_out, and_8_out, and_9_out,
       and_10_out, and_11_out, and_12_out, not_1_out, not_2_out, not_3_out, not_4_out, not_5_out, not_6_out,
       or_1_out, or_2_out, or_3_out, or_4_out, or_5_out, or_6_out, or_7_out, or_8_out;

  not not_1 (not_1_out, LD);
  not not_2 (not_2_out, not_1_out);
  and and_1 (and_1_out, INC, not_1_out);
  not not_3 (not_3_out, L_NPUT[0]);
  not not_4 (not_4_out, L_NPUT[1]);
  not not_5 (not_5_out, L_NPUT[2]);
  not not_6 (not_6_out, L_NPUT[3]);
  and and_2 (and_2_out, not_2_out, L_NPUT[0]);
  and and_3 (and_3_out, not_2_out, not_3_out);
  and and_4 (and_4_out, not_2_out, L_NPUT[1]);
  and and_5 (and_5_out, not_2_out, not_4_out);
  and and_6 (and_6_out, not_2_out, L_NPUT[2]);
  and and_7 (and_7_out, not_2_out, not_5_out);
  and and_8 (and_8_out, not_2_out, L_NPUT[3]);
  and and_9 (and_9_out, not_2_out, not_6_out);
  and and_10 (and_10_out, and_1_out, OUTPUT[0]);
  and and_11 (and_11_out, and_1_out, OUTPUT[0], OUTPUT[1]);
  or or_1 (or_1_out, and_1_out, and_2_out);
  or or_2 (or_2_out, and_1_out, and_3_out);
  or or_3 (or_3_out, and_4_out, and_10_out);
  or or_4 (or_4_out, and_10_out, and_5_out);
  or or_5 (or_5_out, and_6_out, and_11_out);
  or or_6 (or_6_out, and_11_out, and_7_out);
  and and_12 (and_12_out, OUTPUT[2], OUTPUT[1], OUTPUT[0], and_1_out);
  or or_7 (or_7_out, and_8_out, and_12_out);
  or or_8 (or_8_out, and_12_out, and_9_out);
  J_K_Flip_Flop j_k_ff_1 (.J(or_1_out), .clk(CLK), .K(or_2_out), .Q(OUTPUT[0]), .reset(CLR));  // open: Qn, preset
  J_K_Flip_Flop j_k_ff_2 (.K(CLR), .preset(OUTPUT[1]), .reset(OUTPUT[1]));  // open: J, clk, Q, Qn
  J_K_Flip_Flop j_k_ff_3 (.J(or_5_out), .clk(CLK), .K(or_6_out), .Q(OUTPUT[2]), .reset(CLR));  // open: Qn, preset
  J_K_Flip_Flop j_k_ff_4 (.J(or_7_out), .clk(CLK), .K(or_8_out), .Q(OUTPUT[3]), .reset(CLR));  // open: Qn, preset
  and and_13 (elde, OUTPUT[0], OUTPUT[1], OUTPUT[3], OUTPUT[2]);
endmodule

module register_8bit (
  input  [7:0] L_NPUT,
  input  CLK,
  input  LOAD,
  output [7:0] OUTPUT
);

  register_4bit register_4bit_1 (
    .CLK(CLK), .L_NPUT(L_NPUT[3:0]), .LD(LOAD), .OUTPUT(OUTPUT[3:0]));  // open: elde, INC, CLR
  register_4bit register_4bit_2 (
    .CLK(CLK), .L_NPUT(L_NPUT[7:4]), .LD(LOAD), .OUTPUT(OUTPUT[7:4]));  // open: elde, INC, CLR
endmodule

module register_12bit (
  input  [11:0] L_NPUT,
  input  LD,
  input  CLK,
  input  INC,
  input  CLR,
  output [11:0] OUTPUT
);

  wire and_1_out, and_2_out, register_4bit_1_elde, register_4bit_2_elde;

  register_4bit register_4bit_1 (
    .CLK(CLK), .elde(register_4bit_1_elde), .L_NPUT(L_NPUT[3:0]), .INC(INC), .LD(LD), .CLR(CLR),
    .OUTPUT(OUTPUT[3:0]));
  register_4bit register_4bit_2 (
    .CLK(CLK), .elde(register_4bit_2_elde), .L_NPUT(L_NPUT[7:4]), .INC(and_1_out), .LD(LD), .CLR(CLR),
    .OUTPUT(OUTPUT[7:4]));
  and and_1 (and_1_out, INC, register_4bit_1_elde);
  register_4bit register_4bit_3 (
    .CLK(CLK), .L_NPUT(L_NPUT[11:8]), .INC(and_2_out), .LD(LD), .CLR(CLR), .OUTPUT(OUTPUT[11:8]));  // open: elde
  and and_2 (and_2_out, INC, register_4bit_2_elde);
endmodule

module register_16bit (
  input  [15:0] L_NPUT,
  input  INC,
  input  CLK,
  input  LD,
  input  CLR,
  output [15:0] OUTPUT
);

  register_4bit register_4bit_1 (
    .CLK(CLK), .L_NPUT(L_NPUT[3:0]), .INC(INC), .LD(LD), .CLR(CLR), .OUTPUT(OUTPUT[3:0]));  // open: elde
  register_4bit register_4bit_2 (
    .CLK(CLK), .L_NPUT(L_NPUT[7:4]), .INC(INC), .LD(LD), .CLR(CLR), .OUTPUT(OUTPUT[7:4]));  // open: elde
  register_4bit register_4bit_3 (
    .CLK(CLK), .L_NPUT(L_NPUT[11:8]), .LD(LD), .CLR(CLR), .OUTPUT(OUTPUT[11:8]));  // open: elde, INC
  register_4bit register_4bit_4 (
    .CLK(CLK), .L_NPUT(L_NPUT[15:12]), .INC(INC), .LD(LD), .CLR(CLR), .OUTPUT(OUTPUT[15:12]));  // open: elde
endmodule

module alu_1bit (
  input  INPR,
  input  DR,
  input  AC,
  input  in_4,
  input  Cin,
  input  ADD,
  input  CMA,
  input  in_8,
  input  LD_INPR,
  input  CIR,
  input  AC_i_plus_1,
  input  CIL,
  input  AC_i_minus_1,
  output Cout,
  output AC_OUTPUT
);

  wire adder_1_out, and_2_out, and_3_out, and_4_out, AND_out, LD_DR_out, not_1_out, SHL_out, SHR_out;

  Adder #(.width(1)) adder_1 (.a(AC), .b(DR), .out(adder_1_out), .cin(Cin), .cout(Cout));
  not not_1 (not_1_out, AC);
  and AND (AND_out, in_4, AC, DR);
  and and_2 (and_2_out, ADD, adder_1_out);
  and and_3 (and_3_out, CMA, not_1_out);
  and LD_DR (LD_DR_out, in_8, DR);
  and and_4 (and_4_out, LD_INPR, INPR);
  and SHR (SHR_out, CIR, AC_i_plus_1);
  and SHL (SHL_out, CIL, AC_i_minus_1);
  or or_1 (AC_OUTPUT, AND_out, and_2_out, and_3_out, LD_DR_out, and_4_out, SHR_out, SHL_out);
endmodule

// ALU
module alu_16bit (
  input  [15:0] AC,
  input  [15:0] DR,
  input  [7:0] INPR,
  input  AND,
  input  ADD,
  input  CMA,
  input  LD_DR,
  input  LD_INPR,
  input  CIR,
  input  CIL,
  input  CLA,
  input  CME,
  input  CLOCK,
  output [15:0] out_14,
  output OUTPUT
);

  wire alu_1bit_1_cout, alu_1bit_2_cout, alu_1bit_3_cout, alu_1bit_4_cout, alu_1bit_5_cout, alu_1bit_6_cout,
       alu_1bit_7_cout, alu_1bit_8_cout, alu_1bit_9_cout, alu_1bit_10_cout, alu_1bit_11_cout,
       alu_1bit_12_cout, alu_1bit_13_cout, alu_1bit_14_cout, alu_1bit_15_cout, alu_1bit_16_cout,
       carry_logic_1_cin, carry_logic_1_i_minus_1, carry_logic_1_i_plus_1;

  // Probe on AC
  // Probe on DR
  // Probe on INPR
  alu_1bit alu_1bit_1 (
    .in_4(AND), .ADD(ADD), .CMA(CMA), .in_8(LD_DR), .LD_INPR(LD_INPR), .CIR(CIR), .CIL(CIL), .INPR(INPR[0]),
    .DR(DR[0]), .AC(AC[0]), .Cin(carry_logic_1_cin), .Cout(alu_1bit_1_cout), .AC_i_plus_1(AC[1]),
    .AC_i_minus_1(carry_logic_1_i_minus_1), .AC_OUTPUT(out_14[0]));
  alu_1bit alu_1bit_2 (
    .in_4(AND), .ADD(ADD), .CMA(CMA), .in_8(LD_DR), .LD_INPR(LD_INPR), .CIR(CIR), .CIL(CIL), .INPR(INPR[1]),
    .DR(DR[1]), .AC(AC[1]), .Cin(alu_1bit_1_cout), .Cout(alu_1bit_2_cout), .AC_i_plus_1(AC[2]),
    .AC_i_minus_1(AC[0]), .AC_OUTPUT(out_14[1]));
  alu_1bit alu_1bit_3 (
    .in_4(AND), .ADD(ADD), .CMA(CMA), .in_8(LD_DR), .LD_INPR(LD_INPR), .CIR(CIR), .CIL(CIL), .INPR(INPR[2]),
    .DR(DR[2]), .AC(AC[2]), .Cin(alu_1bit_2_cout), .Cout(alu_1bit_3_cout), .AC_i_plus_1(AC[3]),
    .AC_i_minus_1(AC[1]), .AC_OUTPUT(out_14[2]));
  alu_1bit alu_1bit_4 (
    .in_4(AND), .ADD(ADD), .CMA(CMA), .in_8(LD_DR), .LD_INPR(LD_INPR), .CIR(CIR), .CIL(CIL), .INPR(INPR[3]),
    .DR(DR[3]), .AC(AC[3]), .Cin(alu_1bit_3_cout), .Cout(alu_1bit_4_cout), .AC_i_plus_1(AC[4]),
    .AC_i_minus_1(AC[2]), .AC_OUTPUT(out_14[3]));
  alu_1bit alu_1bit_5 (
    .in_4(AND), .ADD(ADD), .CMA(CMA), .in_8(LD_DR), .LD_INPR(LD_INPR), .CIR(CIR), .CIL(CIL), .INPR(INPR[4]),
    .DR(DR[4]), .AC(AC[4]), .Cin(alu_1bit_4_cout), .Cout(alu_1bit_5_cout), .AC_i_plus_1(AC[5]),
    .AC_i_minus_1(AC[3]), .AC_OUTPUT(out_14[4]));
  alu_1bit alu_1bit_6 (
    .in_4(AND), .ADD(ADD), .CMA(CMA), .in_8(LD_DR), .LD_INPR(LD_INPR), .CIR(CIR), .CIL(CIL), .INPR(INPR[5]),
    .DR(DR[5]), .AC(AC[5]), .Cin(alu_1bit_5_cout), .Cout(alu_1bit_6_cout), .AC_i_plus_1(AC[6]),
    .AC_i_minus_1(AC[4]), .AC_OUTPUT(out_14[5]));
  alu_1bit alu_1bit_7 (
    .in_4(AND), .ADD(ADD), .CMA(CMA), .in_8(LD_DR), .LD_INPR(LD_INPR), .CIR(CIR), .CIL(CIL), .INPR(INPR[6]),
    .DR(DR[6]), .AC(AC[6]), .Cin(alu_1bit_6_cout), .Cout(alu_1bit_7_cout), .AC_i_plus_1(AC[7]),
    .AC_i_minus_1(AC[5]), .AC_OUTPUT(out_14[6]));
  alu_1bit alu_1bit_8 (
    .in_4(AND), .ADD(ADD), .CMA(CMA), .in_8(LD_DR), .LD_INPR(LD_INPR), .CIR(CIR), .CIL(CIL), .INPR(INPR[7]),
    .DR(DR[7]), .AC(AC[7]), .Cin(alu_1bit_7_cout), .Cout(alu_1bit_8_cout), .AC_i_plus_1(AC[8]),
    .AC_i_minus_1(AC[6]), .AC_OUTPUT(out_14[7]));
  alu_1bit alu_1bit_9 (
    .in_4(AND), .ADD(ADD), .CMA(CMA), .in_8(LD_DR), .LD_INPR(LD_INPR), .CIR(CIR), .CIL(CIL), .INPR(1'b0),
    .DR(DR[8]), .AC(AC[8]), .Cin(alu_1bit_8_cout), .Cout(alu_1bit_9_cout), .AC_i_plus_1(AC[9]),
    .AC_i_minus_1(AC[7]), .AC_OUTPUT(out_14[8]));
  alu_1bit alu_1bit_10 (
    .in_4(AND), .ADD(ADD), .CMA(CMA), .in_8(LD_DR), .LD_INPR(LD_INPR), .CIR(CIR), .CIL(CIL), .INPR(1'b0),
    .DR(DR[9]), .AC(AC[9]), .Cin(alu_1bit_9_cout), .Cout(alu_1bit_10_cout), .AC_i_plus_1(AC[10]),
    .AC_i_minus_1(AC[8]), .AC_OUTPUT(out_14[9]));
  alu_1bit alu_1bit_11 (
    .in_4(AND), .ADD(ADD), .CMA(CMA), .in_8(LD_DR), .LD_INPR(LD_INPR), .CIR(CIR), .CIL(CIL), .INPR(1'b0),
    .DR(DR[10]), .AC(AC[10]), .Cin(alu_1bit_10_cout), .Cout(alu_1bit_11_cout), .AC_i_plus_1(AC[11]),
    .AC_i_minus_1(AC[9]), .AC_OUTPUT(out_14[10]));
  alu_1bit alu_1bit_12 (
    .in_4(AND), .ADD(ADD), .CMA(CMA), .in_8(LD_DR), .LD_INPR(LD_INPR), .CIR(CIR), .CIL(CIL), .INPR(1'b0),
    .DR(DR[11]), .AC(AC[11]), .Cin(alu_1bit_11_cout), .Cout(alu_1bit_12_cout), .AC_i_plus_1(AC[12]),
    .AC_i_minus_1(AC[10]), .AC_OUTPUT(out_14[11]));
  alu_1bit alu_1bit_13 (
    .in_4(AND), .ADD(ADD), .CMA(CMA), .in_8(LD_DR), .LD_INPR(LD_INPR), .CIR(CIR), .CIL(CIL), .INPR(1'b0),
    .DR(DR[12]), .AC(AC[12]), .Cin(alu_1bit_12_cout), .Cout(alu_1bit_13_cout), .AC_i_plus_1(AC[13]),
    .AC_i_minus_1(AC[11]), .AC_OUTPUT(out_14[12]));
  alu_1bit alu_1bit_14 (
    .in_4(AND), .ADD(ADD), .CMA(CMA), .in_8(LD_DR), .LD_INPR(LD_INPR), .CIR(CIR), .CIL(CIL), .INPR(1'b0),
    .DR(DR[13]), .AC(AC[13]), .Cin(alu_1bit_13_cout), .Cout(alu_1bit_14_cout), .AC_i_plus_1(AC[14]),
    .AC_i_minus_1(AC[12]), .AC_OUTPUT(out_14[13]));
  alu_1bit alu_1bit_15 (
    .in_4(AND), .ADD(ADD), .CMA(CMA), .in_8(LD_DR), .LD_INPR(LD_INPR), .CIR(CIR), .CIL(CIL), .INPR(1'b0),
    .DR(DR[14]), .AC(AC[14]), .Cin(alu_1bit_14_cout), .Cout(alu_1bit_15_cout), .AC_i_plus_1(AC[15]),
    .AC_i_minus_1(AC[13]), .AC_OUTPUT(out_14[14]));
  alu_1bit alu_1bit_16 (
    .in_4(AND), .ADD(ADD), .CMA(CMA), .in_8(LD_DR), .LD_INPR(LD_INPR), .CIR(CIR), .CIL(CIL), .INPR(1'b0),
    .DR(DR[15]), .AC(AC[15]), .Cin(alu_1bit_15_cout), .Cout(alu_1bit_16_cout),
    .AC_i_plus_1(carry_logic_1_i_plus_1), .AC_i_minus_1(AC[14]), .AC_OUTPUT(out_14[15]));
  // Probe on out_14
  carry_logic carry_logic_1 (
    .Cout(alu_1bit_16_cout), .ADD(ADD), .AC_0(carry_logic_1_i_minus_1), .CIR(CIR),
    .AC_15(carry_logic_1_i_plus_1), .CIL(CIL), .CME(CME), .CLK(CLOCK), .CLE(CLA), .OUTPUT(OUTPUT),
    .i_minus_1(carry_logic_1_i_minus_1), .i_plus_1(carry_logic_1_i_plus_1), .Cin(carry_logic_1_cin));
endmodule

module counter (
  input  CLK,
  input  SC_CLEAR,
  output [3:0] OUTPUT
);

  wire and_1_out, register_1_q;

  Counter #(.max('hf), .width(4)) counter_1 (
    .count(1'b1), .Q(OUTPUT), .clk(CLK), .clr(register_1_q));  // open: load, D, carry, up
  Register #(.width(1)) register_1 (.D(SC_CLEAR), .Q(register_1_q), .clk(CLK), .clr(and_1_out));  // open: en
  and and_1 (and_1_out, CLK, SC_CLEAR);
endmodule

module PC_KONTROL_BUF (
  input  I,
  input  in_2,
  input  D4,
  input  D5,
  input  D6,
  input  D7,
  input  T0,
  input  T1,
  input  T2,
  input  T3,
  input  T4,
  input  T5,
  input  T6,
  input  IR1,
  input  IR2,
  input  IR3,
  input  IR4,
  input  IR8,
  input  IR9,
  input  DR,
  input  in_21,
  input  AC_15,
  input  AC,
  input  E,
  input  FGI,
  input  FGO,
  output PC_LD,
  output PC_INC,
  output PC_CLR,
  output PC_BUS
);

  wire and_1_out, and_2_out, and_3_out, and_4_out, and_5_out, and_6_out, and_7_out, and_8_out, and_9_out,
       and_10_out, and_11_out, and_12_out, and_13_out, and_15_out, and_16_out, and_17_out, and_18_out,
       controlled_buffer_1_out, controlled_buffer_2_out, controlled_buffer_3_out, controlled_buffer_4_out,
       controlled_buffer_5_out, controlled_buffer_6_out, controlled_buffer_7_out, not_1_out, not_2_out,
       not_3_out, not_4_out, not_5_out, not_6_out, not_7_out, not_8_out, not_9_out, not_10_out, or_1_out,
       p_out, r_out;

  not not_1 (not_1_out, in_2);
  not not_2 (not_2_out, I);
  not not_3 (not_3_out, I);
  not not_4 (not_4_out, I);
  not not_5 (not_5_out, I);
  and and_1 (and_1_out, not_1_out, T1);
  and and_2 (and_2_out, in_2, T2);
  and and_3 (and_3_out, T6, D6);
  and and_4 (and_4_out, D7, T3, not_2_out);
  and and_5 (and_5_out, T3, D7, not_3_out);
  and r (r_out, T3, not_4_out, D7);
  and and_6 (and_6_out, D7, T3, not_5_out);
  and and_7 (and_7_out, I, D7, T3);
  and p (p_out, T3, D7, I);
  assign controlled_buffer_1_out = not_6_out ? and_3_out : 1'bz;  // Controlled_Buffer controlled_buffer_1
  not not_6 (not_6_out, DR);
  and and_8 (and_8_out, and_4_out, IR4);
  and and_9 (and_9_out, and_5_out, IR3);
  and and_10 (and_10_out, r_out, IR2);
  and and_11 (and_11_out, and_6_out, IR1);
  and and_12 (and_12_out, and_7_out, IR9);
  and and_13 (and_13_out, p_out, IR8);
  and and_14 (PC_CLR, T1, in_2);
  or or_1 (or_1_out, in_2, not_7_out);
  not not_7 (not_7_out, in_2);
  and and_15 (and_15_out, D4, T4);
  and and_16 (and_16_out, T5, D5);
  assign controlled_buffer_2_out = not_8_out ? and_8_out : 1'bz;  // Controlled_Buffer controlled_buffer_2
  not not_8 (not_8_out, in_21);
  assign controlled_buffer_3_out = AC_15 ? and_9_out : 1'bz;  // Controlled_Buffer controlled_buffer_3
  assign controlled_buffer_4_out = not_9_out ? and_10_out : 1'bz;  // Controlled_Buffer controlled_buffer_4
  not not_9 (not_9_out, AC);
  assign controlled_buffer_5_out = not_10_out ? and_11_out : 1'bz;  // Controlled_Buffer controlled_buffer_5
  not not_10 (not_10_out, E);
  assign controlled_buffer_6_out = FGI ? and_12_out : 1'bz;  // Controlled_Buffer controlled_buffer_6
  assign controlled_buffer_7_out = FGO ? and_13_out : 1'bz;  // Controlled_Buffer controlled_buffer_7
  and and_17 (and_17_out, or_1_out, T0);
  and and_18 (and_18_out, T4, D5);
  or or_2 (PC_LD, and_15_out, and_16_out);
  or or_3 (PC_BUS, and_17_out, and_18_out);
  or or_4 (PC_INC, and_1_out, and_2_out, controlled_buffer_1_out, controlled_buffer_2_out, controlled_buffer_3_out, controlled_buffer_4_out, controlled_buffer_5_out, controlled_buffer_6_out, controlled_buffer_7_out);
endmodule

module S_kontrol (
  input  D7,
  input  I,
  input  T3,
  input  IR0,
  output S_CLR
);

  wire not_1_out;

  not not_1 (not_1_out, I);
  and and_1 (S_CLR, IR0, T3, not_1_out, D7);
endmodule

module I_kontrol (
  input  R,
  input  T2,
  input  in_3,
  output out_4
);

  wire and_1_out, not_1_out;

  not not_1 (not_1_out, R);
  and and_1 (and_1_out, not_1_out, T2);
  // T_Flip_Flop t_ff_1: pin names not known; wires that end beside it: in_3, and_1_out, out_4
endmodule

module carry_logic (
  input  Cout,
  input  ADD,
  input  AC_0,
  input  CIR,
  input  AC_15,
  input  CIL,
  input  CME,
  input  CLK,
  input  CLE,
  output OUTPUT,
  output i_minus_1,
  output i_plus_1,
  output Cin
);

  wire and_1_out, and_2_out, and_3_out, and_4_out, and_5_out, and_6_out, and_7_out, and_8_out, and_9_out,
       and_10_out, and_11_out, not_1_out, or_1_out, or_2_out, or_3_out, or_4_out, or_5_out, or_6_out,
       or_7_out, undriven;

  and and_1 (and_1_out, Cout, ADD);
  and and_2 (and_2_out, AC_0, CIR);
  or or_1 (or_1_out, and_1_out, and_2_out, and_3_out);
  and and_3 (and_3_out, AC_15, CIL);
  or or_2 (or_2_out, Cout, AC_0, AC_15);
  and and_4 (and_4_out, ~AC_15, ~AC_0, ~Cout);  // AND_Gate
  and and_5 (and_5_out, and_4_out, or_3_out);
  or or_3 (or_3_out, CIL, CIR, ADD);
  not not_1 (not_1_out, or_1_out);
  and and_6 (and_6_out, or_1_out, or_2_out);
  and and_7 (and_7_out, or_2_out, not_1_out);
  and and_8 (and_8_out, ~and_5_out, and_6_out);  // AND_Gate
  and and_9 (and_9_out, ~and_5_out, and_7_out);  // AND_Gate
  and and_10 (and_10_out, 1'b0, and_5_out);
  and and_11 (and_11_out, 1'b1, and_5_out);
  or or_4 (or_4_out, and_8_out, and_10_out);
  or or_5 (or_5_out, and_9_out, and_11_out);
  or or_6 (or_6_out, or_4_out, CME);
  or or_7 (or_7_out, or_5_out, CME);
  J_K_Flip_Flop NEXT_STATE (.K(CLE), .clk(CLE), .preset(OUTPUT));  // open: J, Q, Qn, reset
  D_Flip_Flop PREV_STATE (.clk(CLE), .preset(undriven));  // open: D, Q, Qn, reset
  and and_12 (i_minus_1, undriven, and_3_out);
  and and_13 (i_plus_1, undriven, and_2_out);
  and and_14 (Cin, undriven, and_1_out);
endmodule
