// Logisim project 32_bit_computer.circ as structural Verilog: 6 circuits, main circuit main
module branch_eval (
  input  Branch,
  input  [2:0] funct3,
  input  Zero,
  input  Less,
  input  LessU,
  output BranchTaken
);

  wire multiplexer_1_out, not_1_out, not_2_out, not_3_out;

  not not_1 (not_1_out, Zero);
  not not_2 (not_2_out, Less);
  not not_3 (not_3_out, LessU);
  Multiplexer #(.select(3), .width(1)) multiplexer_1 (
    .in0(Zero), .in1(not_1_out), .in2(1'b0), .in3(1'b0), .in4(Less), .in5(not_2_out), .in6(LessU),
    .in7(not_3_out), .out(multiplexer_1_out), .sel(funct3));
  and and_1 (BranchTaken, Branch, multiplexer_1_out);
endmodule

module alu_32bit (
  input  [31:0] A,
  input  [31:0] B,
  input  [3:0] ALUControl,
  output Less,
  output LessU,
  output Sign,
  output [31:0] ALUResult,
  output Zero
);

  wire [4:0] undriven_18, undriven_19, undriven_20;
  wire [31:0] adder_1_out, and_1_out, bit_extender_1_out, or_1_out, shifter_1_out, shifter_2_out,
       shifter_3_out, subtractor_1_out, undriven, undriven_2, undriven_3, undriven_4, undriven_5, undriven_6,
       undriven_7, undriven_8, undriven_9, undriven_10, undriven_11, undriven_12, undriven_13, undriven_14,
       undriven_15, undriven_16, undriven_17, undriven_21, undriven_22, undriven_23, undriven_24, xor_1_out;

  Adder #(.width(32)) adder_1 (.a(undriven), .b(undriven_11), .out(adder_1_out));  // open: cin, cout
  Subtractor #(.width(32)) subtractor_1 (.a(undriven_2), .b(undriven_12), .out(subtractor_1_out));  // open: bin, bout
  Shifter #(.shift("ll"), .width(32)) shifter_1 (.in(undriven_3), .\dist (undriven_18), .out(shifter_1_out));
  Comparator #(.mode("twosComplement"), .width(32)) comparator_1 (
    .a(undriven_4), .b(undriven_13), .lt(Less));  // open: gt, eq
  Comparator #(.mode("unsigned"), .width(32)) comparator_2 (
    .a(undriven_5), .b(undriven_14), .lt(LessU));  // open: gt, eq
  assign xor_1_out = undriven_6 ^ undriven_15;  // XOR_Gate xor_1, 32 bits wide
  Shifter #(.shift("lr"), .width(32)) shifter_2 (.in(undriven_7), .\dist (undriven_19), .out(shifter_2_out));
  Shifter #(.shift("ar"), .width(32)) shifter_3 (.in(undriven_8), .\dist (undriven_20), .out(shifter_3_out));
  assign or_1_out = undriven_9 | undriven_16;  // OR_Gate or_1, 32 bits wide
  assign and_1_out = undriven_10 & undriven_17;  // AND_Gate and_1, 32 bits wide
  assign bit_extender_1_out = {{31{1'b0}}, Less};  // Bit_Extender bit_extender_1
  assign bit_extender_1_out = {{31{1'b0}}, LessU};  // Bit_Extender bit_extender_2
  Multiplexer #(.select(4), .width(32)) multiplexer_1 (
    .in0(adder_1_out), .in1(subtractor_1_out), .in2(shifter_1_out), .in3(bit_extender_1_out),
    .in4(bit_extender_1_out), .in5(xor_1_out), .in6(shifter_2_out), .in7(shifter_3_out), .in8(or_1_out),
    .in9(and_1_out), .in10({32{1'b0}}), .in11(undriven_21), .in12(undriven_22), .in13(undriven_23),
    .in14(undriven_24), .in15({32{1'b0}}), .out(ALUResult), .sel(ALUControl));
  Comparator #(.width(32)) comparator_3 (.a(ALUResult), .b({32{1'b0}}), .eq(Zero));  // open: gt, lt

  assign Sign = ALUResult[31];
endmodule

module imm_gen (
  input  [31:0] inst,
  input  [2:0] ImmSel,
  output [31:0] imm
);

  wire [19:0] undriven_4;
  wire [31:0] bit_extender_1_out, bit_extender_2_out, bit_extender_3_out, bit_extender_4_out;
  wire [31:7] undriven, undriven_2;
  wire [31:12] undriven_3;

  assign bit_extender_1_out = {{20{inst[31]}}, inst[31:20]};  // Bit_Extender bit_extender_1
  assign bit_extender_2_out = {{20{undriven[31]}}, {undriven[31:25], undriven[11:7]}};  // Bit_Extender bit_extender_2
  assign bit_extender_3_out = {{19{undriven_2[31]}}, {undriven_2[31], undriven_2[7], undriven_2[30:25], undriven_2[11:8], 1'b0}};  // Bit_Extender bit_extender_3
  assign bit_extender_4_out = {{11{undriven_3[31]}}, {undriven_3[31], undriven_3[19:12], undriven_3[20], undriven_3[30:21], 1'b0}};  // Bit_Extender bit_extender_4
  Multiplexer #(.select(3), .width(32)) multiplexer_1 (
    .in0(bit_extender_1_out), .in1(bit_extender_2_out), .in2(bit_extender_3_out),
    .in3({undriven_4, {12{1'b0}}}), .in4(bit_extender_4_out), .in5({32{1'b0}}), .in6({32{1'b0}}),
    .in7({32{1'b0}}), .out(imm), .sel(ImmSel));
endmodule

module control_unit (
  input  [6:0] opcode,
  input  [2:0] funct3,
  input  [6:0] funct7,
  output RegWrite,
  output ALUSrc,
  output MemWrite,
  output MemRead,
  output Branch,
  output [1:0] MemToReg,
  output Jump,
  output JALR,
  output [2:0] ImmSel,
  output AUIPC,
  output [3:0] ALUControl
);

  wire and_1_out, comparator_1_eq, comparator_2_eq, undriven_4;
  wire [0:0] or_8_out;
  wire [3:0] bit_extender_1_out, multiplexer_1_out, multiplexer_2_out;
  wire [6:0] undriven, undriven_2, undriven_3, undriven_5, undriven_6, undriven_7, undriven_8, undriven_9,
       undriven_10;

  Comparator #(.width(7)) comparator_1 (.a(undriven), .b(7'b0110011), .eq(comparator_1_eq));  // open: gt, lt
  Comparator #(.width(7)) comparator_2 (.a(undriven_2), .b(7'b0010011), .eq(comparator_2_eq));  // open: gt, lt
  Comparator #(.width(7)) comparator_3 (.a(undriven_3), .b(7'b0000011), .eq(MemRead));  // open: gt, lt
  Comparator #(.width(7)) comparator_4 (.a(undriven_5), .b(7'b0100011), .eq(MemWrite));  // open: gt, lt
  Comparator #(.width(7)) comparator_5 (.a(undriven_6), .b(7'b1100011), .eq(Branch));  // open: gt, lt
  Comparator #(.width(7)) comparator_6 (.a(undriven_7), .b(7'b1101111), .eq(ImmSel[2]));  // open: gt, lt
  Comparator #(.width(7)) comparator_7 (.a(undriven_8), .b(7'b1100111), .eq(JALR));  // open: gt, lt
  Comparator #(.width(7)) comparator_8 (.a(undriven_9), .b(7'b0110111), .eq(AUIPC));  // open: gt, lt
  Comparator #(.width(7)) comparator_9 (.a(undriven_10), .b(7'b0010111), .eq(AUIPC));  // open: gt, lt
  and and_1 (and_1_out, comparator_1_eq, undriven_4);
  assign bit_extender_1_out = {{3{1'b0}}, and_1_out};  // Bit_Extender bit_extender_1
  Multiplexer #(.width(4)) multiplexer_1 (.in0(4'b0110), .in1(4'b0111), .out(multiplexer_1_out), .sel(undriven_4));
  or or_1 (RegWrite, comparator_1_eq, comparator_2_eq, MemRead, ImmSel[2], JALR, AUIPC);
  or or_2 (ALUSrc, comparator_2_eq, MemRead, MemWrite, AUIPC, AUIPC);
  or or_3 (Jump, ImmSel[2], JALR);
  Multiplexer #(.select(3), .width(4)) multiplexer_2 (
    .in0(bit_extender_1_out), .in1(4'b0010), .in2(4'b0011), .in3(4'b0100), .in4(4'b0101),
    .in5(multiplexer_1_out), .in6(4'b1000), .in7(4'b1001), .out(multiplexer_2_out), .sel(funct3));
  or or_4 (MemToReg[0], MemRead, AUIPC);
  or or_5 (MemToReg[1], ImmSel[2], JALR, AUIPC);
  or or_6 (ImmSel[0], MemWrite, AUIPC, AUIPC);
  or or_7 (ImmSel[1], Branch, AUIPC, AUIPC);
  or or_8 (or_8_out[0], comparator_1_eq, comparator_2_eq);
  Multiplexer #(.select(2), .width(4)) multiplexer_3 (
    .in0(4'b0000), .in1(multiplexer_2_out), .in2(4'b0001), .in3(4'b0000), .out(ALUControl),
    .sel({Branch, or_8_out[0]}));
endmodule

module register_file (
  input  [4:0] ReadReg1,
  input  [4:0] ReadReg2,
  input  [4:0] WriteReg,
  input  [31:0] WriteData,
  input  RegWrite,
  input  Clock,
  input  Reset,
  output [31:0] x1_val,
  output [31:0] x2_val,
  output [31:0] x3_val,
  output [31:0] x4_val,
  output [31:0] ReadData1,
  output [31:0] ReadData2
);

  wire decoder_1_out1, decoder_1_out2, decoder_1_out3, decoder_1_out4, decoder_1_out5, decoder_1_out6,
       decoder_1_out7, decoder_1_out8, decoder_1_out9, decoder_1_out10, decoder_1_out11, decoder_1_out12,
       decoder_1_out13, decoder_1_out14, decoder_1_out15, decoder_1_out16, decoder_1_out17, decoder_1_out18,
       decoder_1_out19, decoder_1_out20, decoder_1_out21, decoder_1_out22, decoder_1_out23, decoder_1_out24,
       decoder_1_out25, decoder_1_out26, decoder_1_out27, decoder_1_out28, decoder_1_out29, decoder_1_out30,
       decoder_1_out31, undriven_32, undriven_33, undriven_34, undriven_35, undriven_36, undriven_37,
       undriven_38, undriven_39, undriven_40, undriven_41, undriven_42, undriven_43, undriven_44,
       undriven_45, undriven_46, undriven_47, undriven_48, undriven_49, undriven_50, undriven_51,
       undriven_52, undriven_53, undriven_54, undriven_55, undriven_56, undriven_57, undriven_58,
       undriven_59, undriven_60, undriven_61, undriven_62, undriven_63, undriven_64, undriven_65,
       undriven_66, undriven_67, undriven_68, undriven_69, undriven_70, undriven_71, undriven_72,
       undriven_73, undriven_74, undriven_75, undriven_76, undriven_77, undriven_78, undriven_79,
       undriven_80, undriven_81, undriven_82, undriven_83, undriven_84, undriven_85, undriven_86,
       undriven_87, undriven_88, undriven_89, undriven_90, undriven_91, undriven_92, undriven_93;
  wire [31:0] register_5_q, register_6_q, register_7_q, register_8_q, register_9_q, register_10_q,
       register_11_q, register_12_q, register_13_q, register_14_q, register_15_q, register_16_q,
       register_17_q, register_18_q, register_19_q, register_20_q, register_21_q, register_22_q,
       register_23_q, register_24_q, register_25_q, register_26_q, register_27_q, register_28_q,
       register_29_q, register_30_q, register_31_q, undriven, undriven_2, undriven_3, undriven_4, undriven_5,
       undriven_6, undriven_7, undriven_8, undriven_9, undriven_10, undriven_11, undriven_12, undriven_13,
       undriven_14, undriven_15, undriven_16, undriven_17, undriven_18, undriven_19, undriven_20,
       undriven_21, undriven_22, undriven_23, undriven_24, undriven_25, undriven_26, undriven_27,
       undriven_28, undriven_29, undriven_30, undriven_31;

  Decoder #(.select(5)) decoder_1 (
    .out1(decoder_1_out1), .out2(decoder_1_out2), .out3(decoder_1_out3), .out4(decoder_1_out4),
    .out5(decoder_1_out5), .out6(decoder_1_out6), .out7(decoder_1_out7), .out8(decoder_1_out8),
    .out9(decoder_1_out9), .out10(decoder_1_out10), .out11(decoder_1_out11), .out12(decoder_1_out12),
    .out13(decoder_1_out13), .out14(decoder_1_out14), .out15(decoder_1_out15), .out16(decoder_1_out16),
    .out17(decoder_1_out17), .out18(decoder_1_out18), .out19(decoder_1_out19), .out20(decoder_1_out20),
    .out21(decoder_1_out21), .out22(decoder_1_out22), .out23(decoder_1_out23), .out24(decoder_1_out24),
    .out25(decoder_1_out25), .out26(decoder_1_out26), .out27(decoder_1_out27), .out28(decoder_1_out28),
    .out29(decoder_1_out29), .out30(decoder_1_out30), .out31(decoder_1_out31), .sel(WriteReg), .en(RegWrite));  // open: out0
  Register #(.width(32)) register_1 (
    .D(undriven), .en(decoder_1_out1), .clk(undriven_32), .Q(x1_val), .clr(undriven_63));
  Register #(.width(32)) register_2 (
    .D(undriven_2), .en(decoder_1_out2), .clk(undriven_33), .Q(x2_val), .clr(undriven_64));
  Register #(.width(32)) register_3 (
    .D(undriven_3), .en(decoder_1_out3), .clk(undriven_34), .Q(x3_val), .clr(undriven_65));
  Register #(.width(32)) register_4 (
    .D(undriven_4), .en(decoder_1_out4), .clk(undriven_35), .Q(x4_val), .clr(undriven_66));
  Register #(.width(32)) register_5 (
    .D(undriven_5), .en(decoder_1_out5), .clk(undriven_36), .Q(register_5_q), .clr(undriven_67));
  Register #(.width(32)) register_6 (
    .D(undriven_6), .en(decoder_1_out6), .clk(undriven_37), .Q(register_6_q), .clr(undriven_68));
  Register #(.width(32)) register_7 (
    .D(undriven_7), .en(decoder_1_out7), .clk(undriven_38), .Q(register_7_q), .clr(undriven_69));
  Register #(.width(32)) register_8 (
    .D(undriven_8), .en(decoder_1_out8), .clk(undriven_39), .Q(register_8_q), .clr(undriven_70));
  Register #(.width(32)) register_9 (
    .D(undriven_9), .en(decoder_1_out9), .clk(undriven_40), .Q(register_9_q), .clr(undriven_71));
  Register #(.width(32)) register_10 (
    .D(undriven_10), .en(decoder_1_out10), .clk(undriven_41), .Q(register_10_q), .clr(undriven_72));
  Register #(.width(32)) register_11 (
    .D(undriven_11), .en(decoder_1_out11), .clk(undriven_42), .Q(register_11_q), .clr(undriven_73));
  Register #(.width(32)) register_12 (
    .D(undriven_12), .en(decoder_1_out12), .clk(undriven_43), .Q(register_12_q), .clr(undriven_74));
  Register #(.width(32)) register_13 (
    .D(undriven_13), .en(decoder_1_out13), .clk(undriven_44), .Q(register_13_q), .clr(undriven_75));
  Register #(.width(32)) register_14 (
    .D(undriven_14), .en(decoder_1_out14), .clk(undriven_45), .Q(register_14_q), .clr(undriven_76));
  Register #(.width(32)) register_15 (
    .D(undriven_15), .en(decoder_1_out15), .clk(undriven_46), .Q(register_15_q), .clr(undriven_77));
  Register #(.width(32)) register_16 (
    .D(undriven_16), .en(decoder_1_out16), .clk(undriven_47), .Q(register_16_q), .clr(undriven_78));
  Register #(.width(32)) register_17 (
    .D(undriven_17), .en(decoder_1_out17), .clk(undriven_48), .Q(register_17_q), .clr(undriven_79));
  Register #(.width(32)) register_18 (
    .D(undriven_18), .en(decoder_1_out18), .clk(undriven_49), .Q(register_18_q), .clr(undriven_80));
  Register #(.width(32)) register_19 (
    .D(undriven_19), .en(decoder_1_out19), .clk(undriven_50), .Q(register_19_q), .clr(undriven_81));
  Register #(.width(32)) register_20 (
    .D(undriven_20), .en(decoder_1_out20), .clk(undriven_51), .Q(register_20_q), .clr(undriven_82));
  Register #(.width(32)) register_21 (
    .D(undriven_21), .en(decoder_1_out21), .clk(undriven_52), .Q(register_21_q), .clr(undriven_83));
  Register #(.width(32)) register_22 (
    .D(undriven_22), .en(decoder_1_out22), .clk(undriven_53), .Q(register_22_q), .clr(undriven_84));
  Register #(.width(32)) register_23 (
    .D(undriven_23), .en(decoder_1_out23), .clk(undriven_54), .Q(register_23_q), .clr(undriven_85));
  Register #(.width(32)) register_24 (
    .D(undriven_24), .en(decoder_1_out24), .clk(undriven_55), .Q(register_24_q), .clr(undriven_86));
  Register #(.width(32)) register_25 (
    .D(undriven_25), .en(decoder_1_out25), .clk(undriven_56), .Q(register_25_q), .clr(undriven_87));
  Register #(.width(32)) register_26 (
    .D(undriven_26), .en(decoder_1_out26), .clk(undriven_57), .Q(register_26_q), .clr(undriven_88));
  Register #(.width(32)) register_27 (
    .D(undriven_27), .en(decoder_1_out27), .clk(undriven_58), .Q(register_27_q), .clr(undriven_89));
  Register #(.width(32)) register_28 (
    .D(undriven_28), .en(decoder_1_out28), .clk(undriven_59), .Q(register_28_q), .clr(undriven_90));
  Register #(.width(32)) register_29 (
    .D(undriven_29), .en(decoder_1_out29), .clk(undriven_60), .Q(register_29_q), .clr(undriven_91));
  Register #(.width(32)) register_30 (
    .D(undriven_30), .en(decoder_1_out30), .clk(undriven_61), .Q(register_30_q), .clr(undriven_92));
  Register #(.width(32)) register_31 (
    .D(undriven_31), .en(decoder_1_out31), .clk(undriven_62), .Q(register_31_q), .clr(undriven_93));
  Multiplexer #(.select(5), .width(32)) multiplexer_1 (
    .in0({32{1'b0}}), .in1(x1_val), .in2(x2_val), .in3(x3_val), .in4(x4_val), .in5(register_5_q),
    .in6(register_6_q), .in7(register_7_q), .in8(register_8_q), .in9(register_9_q), .in10(register_10_q),
    .in11(register_11_q), .in12(register_12_q), .in13(register_13_q), .in14(register_14_q),
    .in15(register_15_q), .in16(register_16_q), .in17(register_17_q), .in18(register_18_q),
    .in19(register_19_q), .in20(register_20_q), .in21(register_21_q), .in22(register_22_q),
    .in23(register_23_q), .in24(register_24_q), .in25(register_25_q), .in26(register_26_q),
    .in27(register_27_q), .in28(register_28_q), .in29(register_29_q), .in30(register_30_q),
    .in31(register_31_q), .out(ReadData1), .sel(ReadReg1));
  Multiplexer #(.select(5), .width(32)) multiplexer_2 (
    .in0({32{1'b0}}), .in1(x1_val), .in2(x2_val), .in3(x3_val), .in4(x4_val), .in5(register_5_q),
    .in6(register_6_q), .in7(register_7_q), .in8(register_8_q), .in9(register_9_q), .in10(register_10_q),
    .in11(register_11_q), .in12(register_12_q), .in13(register_13_q), .in14(register_14_q),
    .in15(register_15_q), .in16(register_16_q), .in17(register_17_q), .in18(register_18_q),
    .in19(register_19_q), .in20(register_20_q), .in21(register_21_q), .in22(register_22_q),
    .in23(register_23_q), .in24(register_24_q), .in25(register_25_q), .in26(register_26_q),
    .in27(register_27_q), .in28(register_28_q), .in29(register_29_q), .in30(register_30_q),
    .in31(register_31_q), .out(ReadData2), .sel(ReadReg2));
endmodule

module main (
  input  SYS_RESET
);

  wire alu_32bit_1_less, alu_32bit_1_lessu, alu_32bit_1_zero, branch_eval_1_branchtaken,
       control_unit_1_alusrc, control_unit_1_auipc, control_unit_1_branch, control_unit_1_jalr,
       control_unit_1_jump, control_unit_1_memread, control_unit_1_memwrite, control_unit_1_regwrite,
       SYS_CLK_out;
  wire [1:0] control_unit_1_memtoreg;
  wire [2:0] control_unit_1_immsel;
  wire [3:0] control_unit_1_alucontrol;
  wire [9:0] alu_32bit_1_aluresult_2;
  wire [31:0] adder_1_out, adder_2_p3, alu_32bit_1_aluresult, imm_gen_1_imm, multiplexer_1_out,
       multiplexer_2_out, multiplexer_3_out, multiplexer_4_out, multiplexer_5_out, multiplexer_6_out,
       ram_1_dout, register_1_q, register_file_1_readdata1, register_file_1_readdata2,
       register_file_1_x1_val, register_file_1_x2_val, register_file_1_x3_val, register_file_1_x4_val,
       rom_1_data;

  Clock SYS_CLK (.out(SYS_CLK_out));
  Register #(.width(32)) register_1 (
    .D(multiplexer_3_out), .en(1'b1), .clk(SYS_CLK_out), .Q(register_1_q), .clr(SYS_RESET));
  // Probe on register_1_q
  Adder #(.width(32)) adder_1 (.a(register_1_q), .b(32'h4), .out(adder_1_out));  // open: cin, cout
  ROM #(.addrWidth(10), .dataWidth(32)) rom_1 (.addr(register_1_q[11:2]), .data(rom_1_data));
  // Probe on rom_1_data
  control_unit control_unit_1 (
    .opcode(rom_1_data[6:0]), .funct3(rom_1_data[14:12]), .funct7(rom_1_data[31:25]),
    .RegWrite(control_unit_1_regwrite), .ALUSrc(control_unit_1_alusrc), .MemWrite(control_unit_1_memwrite),
    .MemRead(control_unit_1_memread), .MemToReg(control_unit_1_memtoreg),
    .ALUControl(control_unit_1_alucontrol), .Branch(control_unit_1_branch), .Jump(control_unit_1_jump),
    .JALR(control_unit_1_jalr), .ImmSel(control_unit_1_immsel), .AUIPC(control_unit_1_auipc));
  imm_gen imm_gen_1 (.inst(rom_1_data), .ImmSel(control_unit_1_immsel), .imm(imm_gen_1_imm));
  LED REG_WRITE (.in(control_unit_1_regwrite));
  register_file register_file_1 (
    .ReadReg1(rom_1_data[19:15]), .ReadReg2(rom_1_data[24:20]), .WriteReg(rom_1_data[11:7]),
    .WriteData(multiplexer_6_out), .RegWrite(control_unit_1_regwrite), .Clock(SYS_CLK_out),
    .Reset(SYS_RESET), .ReadData1(register_file_1_readdata1), .ReadData2(register_file_1_readdata2),
    .x1_val(register_file_1_x1_val), .x2_val(register_file_1_x2_val), .x3_val(register_file_1_x3_val),
    .x4_val(register_file_1_x4_val));
  // Adder #(.width(32)) adder_2: pin names not known; wires that end beside it: register_1_q, imm_gen_1_imm, adder_2_p3
  Multiplexer #(.width(32)) multiplexer_1 (
    .in0(adder_1_out), .in1(adder_2_p3), .out(multiplexer_1_out), .sel(branch_eval_1_branchtaken));
  Multiplexer #(.width(32)) multiplexer_2 (
    .in0(adder_2_p3),
    .in1({alu_32bit_1_aluresult[31:12], alu_32bit_1_aluresult_2, alu_32bit_1_aluresult[1:0]}),
    .out(multiplexer_2_out), .sel(control_unit_1_jalr));
  Multiplexer #(.width(32)) multiplexer_3 (
    .in0(multiplexer_1_out), .in1(multiplexer_2_out), .out(multiplexer_3_out), .sel(control_unit_1_jump));
  Multiplexer #(.width(32)) multiplexer_4 (
    .in0(register_file_1_readdata1), .in1(register_1_q), .out(multiplexer_4_out), .sel(control_unit_1_auipc));
  Multiplexer #(.width(32)) multiplexer_5 (
    .in0(register_file_1_readdata2), .in1(imm_gen_1_imm), .out(multiplexer_5_out), .sel(control_unit_1_alusrc));
  // Probe on register_file_1_x1_val
  // Probe on register_file_1_x2_val
  // Probe on register_file_1_x3_val
  // Probe on register_file_1_x4_val
  alu_32bit alu_32bit_1 (
    .A(multiplexer_4_out), .B(multiplexer_5_out), .ALUControl(control_unit_1_alucontrol),
    .ALUResult({alu_32bit_1_aluresult[31:12], alu_32bit_1_aluresult_2, alu_32bit_1_aluresult[1:0]}),
    .Zero(alu_32bit_1_zero), .Less(alu_32bit_1_less), .LessU(alu_32bit_1_lessu));  // open: Sign
  RAM #(.addrWidth(10), .dataWidth(32)) ram_1 (
    .addr(alu_32bit_1_aluresult_2), .we(control_unit_1_memwrite), .oe(control_unit_1_memread),
    .clk(SYS_CLK_out), .din(register_file_1_readdata2), .dout(ram_1_dout));
  branch_eval branch_eval_1 (
    .Branch(control_unit_1_branch), .funct3(rom_1_data[14:12]), .Zero(alu_32bit_1_zero),
    .Less(alu_32bit_1_less), .LessU(alu_32bit_1_lessu), .BranchTaken(branch_eval_1_branchtaken));
  LED MEM_WRITE (.in(control_unit_1_memwrite));
  LED BRANCH_TAKEN (.in(branch_eval_1_branchtaken));
  Multiplexer #(.select(2), .width(32)) multiplexer_6 (
    .in0({alu_32bit_1_aluresult[31:12], alu_32bit_1_aluresult_2, alu_32bit_1_aluresult[1:0]}),
    .in1(ram_1_dout), .in2(adder_1_out), .in3(imm_gen_1_imm), .out(multiplexer_6_out),
    .sel(control_unit_1_memtoreg));
endmodule
