// Logisim project 8_bit_computer.circ as structural Verilog: 20 circuits, main circuit main
module main (
  input  [3:0] in_1,
  output out_2
);

  wire clock_1_out, main_kontrol_1_dr_load, main_kontrol_1_hlt, main_kontrol_1_outr, not_1_out;
  wire [1:0] main_kontrol_1_ir_bus_ir_load, main_kontrol_1_m_bus_m_load;
  wire [2:0] main_kontrol_1_ar_bus_ar_inc_ar_load, main_kontrol_1_pc_bus_pc_inc_pc_load;
  wire [3:0] AC_output, alu_4bit_carry_1_ac_output, AR_output, controlled_buffer_1_out,
       controlled_buffer_1_out_2, DR_output, INPR_output, IR_ir_0_3, IR_ir_4_7,
       main_kontrol_1_ac_bus_ac_clear_ac_inc_ac_load, OUTR_output, PC_output;
  wire [6:0] main_kontrol_1_out_11;
  wire [7:0] ram_1_data;

  Clock clock_1 (.out(clock_1_out));
  main_kontrol main_kontrol_1 (
    .IR_4_7(IR_ir_4_7), .CLOCK(main_kontrol_1_ac_bus_ac_clear_ac_inc_ac_load[0]),
    .M_BUS_M_LOAD(main_kontrol_1_m_bus_m_load), .AR_BUS_AR_INC_AR_LOAD(main_kontrol_1_ar_bus_ar_inc_ar_load),
    .PC_BUS_PC_INC_PC_LOAD(main_kontrol_1_pc_bus_pc_inc_pc_load), .DR_LOAD(main_kontrol_1_dr_load),
    .AC_BUS_AC_CLEAR_AC_INC_AC_LOAD(main_kontrol_1_ac_bus_ac_clear_ac_inc_ac_load),
    .OUTR(main_kontrol_1_outr), .IR_BUS_IR_LOAD(main_kontrol_1_ir_bus_ir_load),
    .out_11(main_kontrol_1_out_11), .HLT(main_kontrol_1_hlt));  // open: E_BUS_E_CLEAR_E_LOAD
  not not_1 (not_1_out, main_kontrol_1_hlt);
  and and_1 (main_kontrol_1_ac_bus_ac_clear_ac_inc_ac_load[0], not_1_out, clock_1_out);
  // Probe on INPR_output
  register_4bit INPR (
    .L_nput(in_1), .CLK(main_kontrol_1_ac_bus_ac_clear_ac_inc_ac_load[0]), .\output (INPR_output));  // open: INC, LD, CLR
  alu_4bit_carry alu_4bit_carry_1 (
    .AC(AC_output), .DR(DR_output), .INPR(INPR_output), .AND(main_kontrol_1_out_11[0]),
    .ADD(main_kontrol_1_out_11[1]), .CMA(main_kontrol_1_out_11[2]), .LD_DR(main_kontrol_1_out_11[3]),
    .LD_INPR(main_kontrol_1_out_11[4]), .CIR(main_kontrol_1_out_11[5]), .CIL(main_kontrol_1_out_11[6]),
    .Cout(out_2), .CLK(main_kontrol_1_ac_bus_ac_clear_ac_inc_ac_load[0]),
    .AC_OUTPUT(alu_4bit_carry_1_ac_output));
  RAM #(.addrWidth(4)) ram_1 (
    .addr(AR_output), .data(ram_1_data), .clk(main_kontrol_1_ac_bus_ac_clear_ac_inc_ac_load[0]));  // open: sel, ld, clr
  // Probe on AR_output
  register_4bit AR (
    .L_nput(controlled_buffer_1_out), .CLK(main_kontrol_1_ac_bus_ac_clear_ac_inc_ac_load[0]),
    .INC(main_kontrol_1_ar_bus_ar_inc_ar_load[1]), .LD(main_kontrol_1_ar_bus_ar_inc_ar_load[0]),
    .\output (AR_output));  // open: CLR
  register_4bit PC (
    .L_nput(controlled_buffer_1_out), .CLK(main_kontrol_1_ac_bus_ac_clear_ac_inc_ac_load[0]),
    .INC(main_kontrol_1_pc_bus_pc_inc_pc_load[1]), .LD(main_kontrol_1_pc_bus_pc_inc_pc_load[0]),
    .\output (PC_output));  // open: CLR
  // Probe on DR_output
  register_4bit DR (
    .L_nput(controlled_buffer_1_out), .CLK(main_kontrol_1_ac_bus_ac_clear_ac_inc_ac_load[0]),
    .LD(main_kontrol_1_dr_load), .\output (DR_output));  // open: INC, CLR
  // Probe on AC_output
  register_4bit AC (
    .L_nput(alu_4bit_carry_1_ac_output), .CLK(main_kontrol_1_ac_bus_ac_clear_ac_inc_ac_load[0]),
    .INC(main_kontrol_1_ac_bus_ac_clear_ac_inc_ac_load[1]),
    .LD(main_kontrol_1_ac_bus_ac_clear_ac_inc_ac_load[0]),
    .CLR(main_kontrol_1_ac_bus_ac_clear_ac_inc_ac_load[2]), .\output (AC_output));
  // Probe on OUTR_output
  register_4bit OUTR (
    .L_nput(controlled_buffer_1_out), .CLK(main_kontrol_1_ac_bus_ac_clear_ac_inc_ac_load[0]),
    .LD(main_kontrol_1_outr), .\output (OUTR_output));  // open: INC, CLR
  // Probe on IR_ir_4_7
  // Probe on IR_ir_0_3
  instruction_register IR (
    .L_NPUT({controlled_buffer_1_out_2, controlled_buffer_1_out}),
    .CLK(main_kontrol_1_ac_bus_ac_clear_ac_inc_ac_load[0]), .LD(main_kontrol_1_ir_bus_ir_load[0]),
    .IR_0_3(IR_ir_0_3), .IR_4_7(IR_ir_4_7));
  assign {controlled_buffer_1_out_2, controlled_buffer_1_out} = main_kontrol_1_ar_bus_ar_inc_ar_load[2] ? {4'b0000, AR_output} : 8'bz;  // Controlled_Buffer controlled_buffer_1
  assign {controlled_buffer_1_out_2, controlled_buffer_1_out} = main_kontrol_1_pc_bus_pc_inc_pc_load[2] ? {4'b0000, PC_output} : 8'bz;  // Controlled_Buffer controlled_buffer_2
  assign {controlled_buffer_1_out_2, controlled_buffer_1_out} = main_kontrol_1_ac_bus_ac_clear_ac_inc_ac_load[3] ? {4'b0000, AC_output} : 8'bz;  // Controlled_Buffer controlled_buffer_3
  assign {controlled_buffer_1_out_2, controlled_buffer_1_out} = main_kontrol_1_ir_bus_ir_load[1] ? {4'b0000, IR_ir_0_3} : 8'bz;  // Controlled_Buffer controlled_buffer_4
  assign {controlled_buffer_1_out_2, controlled_buffer_1_out} = main_kontrol_1_m_bus_m_load[1] ? ram_1_data : 8'bz;  // Controlled_Buffer controlled_buffer_5
  // Probe on PC_output

  // Notes on the sheet:
  //   IR(4-7)
  //   ALU
endmodule

// main kontrol
module main_kontrol (
  input  [3:0] IR_4_7,
  input  CLOCK,
  output [1:0] M_BUS_M_LOAD,
  output [2:0] AR_BUS_AR_INC_AR_LOAD,
  output [2:0] PC_BUS_PC_INC_PC_LOAD,
  output DR_LOAD,
  output [3:0] AC_BUS_AC_CLEAR_AC_INC_AC_LOAD,
  output OUTR,
  output [1:0] IR_BUS_IR_LOAD,
  output [2:0] E_BUS_E_CLEAR_E_LOAD,
  output [6:0] out_11,
  output HLT
);

  wire decoder_1_out15, sc_clear_1_out_18;
  wire [1:0] decoder_2_out4;
  wire [2:0] decoder_2_out0;
  wire [3:0] sequence_counter_1_output;
  wire [6:0] decoder_1_out0;
  wire [14:3] decoder_1_out3;

  sc_clear sc_clear_1 (
    .T3(decoder_2_out4[1]), .T4(decoder_2_out4[0]), .D0(decoder_1_out0[0]), .D1(decoder_1_out0[1]),
    .D2(decoder_1_out0[2]), .D3(decoder_1_out3[3]), .D4(decoder_1_out3[4]), .D5(decoder_1_out3[5]),
    .D6(decoder_1_out3[6]), .D7(decoder_1_out3[7]), .D8(decoder_1_out3[8]), .D9(decoder_1_out0[3]),
    .D10(decoder_1_out3[10]), .D11(decoder_1_out0[4]), .D12(decoder_1_out0[5]), .D13(decoder_1_out0[6]),
    .D14(decoder_1_out3[14]), .out_18(sc_clear_1_out_18));
  Decoder #(.select(4)) decoder_1 (
    .out0(decoder_1_out0[0]), .out1(decoder_1_out0[1]), .out2(decoder_1_out0[2]), .out3(decoder_1_out3[3]),
    .out4(decoder_1_out3[4]), .out5(decoder_1_out3[5]), .out6(decoder_1_out3[6]), .out7(decoder_1_out3[7]),
    .out8(decoder_1_out3[8]), .out9(decoder_1_out0[3]), .out10(decoder_1_out3[10]),
    .out11(decoder_1_out0[4]), .out12(decoder_1_out0[5]), .out13(decoder_1_out0[6]),
    .out14(decoder_1_out3[14]), .out15(decoder_1_out15), .sel(IR_4_7));  // open: en
  Decoder #(.select(4)) decoder_2 (
    .out0(decoder_2_out0[0]), .out1(decoder_2_out0[1]), .out2(decoder_2_out0[2]), .out3(decoder_2_out4[1]),
    .out4(decoder_2_out4[0]), .sel(sequence_counter_1_output));  // open: out5, out6, out7, out8, out9, out10, out11, out12, out13, out14, out15, en
  sequence_counter sequence_counter_1 (.CLOCK(CLOCK), .SC_CLEAR(sc_clear_1_out_18), .OUTPUT(sequence_counter_1_output));
  and and_1 (HLT, decoder_2_out4[1], decoder_1_out15);
  ALU alu_1 (
    .T3(decoder_2_out4[1]), .T4(decoder_2_out4[0]), .D0(decoder_1_out0[0]), .D1(decoder_1_out0[1]),
    .D2(decoder_1_out0[2]), .D9(decoder_1_out0[3]), .D11(decoder_1_out0[4]), .D12(decoder_1_out0[5]),
    .D13(decoder_1_out0[6]), .AND(out_11[0]), .ADD(out_11[1]), .CMA(out_11[2]), .DR_LOAD(out_11[3]),
    .LD_INPR(out_11[4]), .CIR(out_11[5]), .CIL(out_11[6]));
  register_kontrol register_kontrol_1 (
    .T0(decoder_2_out0[0]), .T1(decoder_2_out0[1]), .T2(decoder_2_out0[2]), .T3(decoder_2_out4[1]),
    .T4(decoder_2_out4[0]), .D0(decoder_1_out0[0]), .D1(decoder_1_out0[1]), .D2(decoder_1_out0[2]),
    .D3(decoder_1_out3[3]), .D4(decoder_1_out3[4]), .D5(decoder_1_out3[5]), .D6(decoder_1_out3[6]),
    .D7(decoder_1_out3[7]), .D8(decoder_1_out3[8]), .D9(decoder_1_out0[3]), .D10(decoder_1_out3[10]),
    .D11(decoder_1_out0[4]), .D12(decoder_1_out0[5]), .D13(decoder_1_out0[6]), .D14(decoder_1_out3[14]),
    .M_BUS_M_LOAD(M_BUS_M_LOAD), .AR_BUS_AR_INC_AR_LOAD(AR_BUS_AR_INC_AR_LOAD),
    .PC_BUS_PC_INC_PC_LOAD(PC_BUS_PC_INC_PC_LOAD), .DR_LOAD(DR_LOAD),
    .AC_BUS_AC_CLEAR_AC_INC_AC_LOAD(AC_BUS_AC_CLEAR_AC_INC_AC_LOAD), .OUTR_LOAD(OUTR),
    .IR_BUS_IR_LOAD(IR_BUS_IR_LOAD), .E_BUS_E_CLEAR_E_LOAD(E_BUS_E_CLEAR_E_LOAD));

  // Notes on the sheet:
  //   T(3-4)
  //   D(0-14)
  //   SC_CLEAR
  //   D(0-15)
  //   T(0-4)
  //   counter
  //   ALU_KONTROL
  //   T(0-4)
  //   D(0-14)
  //   REGİSTER KONTROL
endmodule

module register_kontrol (
  input  T0,
  input  T1,
  input  T2,
  input  T3,
  input  T4,
  input  D0,
  input  D1,
  input  D2,
  input  D3,
  input  D4,
  input  D5,
  input  D6,
  input  D7,
  input  D8,
  input  D9,
  input  D10,
  input  D11,
  input  D12,
  input  D13,
  input  D14,
  output [1:0] M_BUS_M_LOAD,
  output [2:0] AR_BUS_AR_INC_AR_LOAD,
  output [2:0] PC_BUS_PC_INC_PC_LOAD,
  output DR_LOAD,
  output [3:0] AC_BUS_AC_CLEAR_AC_INC_AC_LOAD,
  output OUTR_LOAD,
  output [1:0] IR_BUS_IR_LOAD,
  output [2:0] E_BUS_E_CLEAR_E_LOAD
);

  OUTR outr_1 (.T3(T3), .D14(D14), .OUTR_LOAD(OUTR_LOAD));
  IR ir_1 (.T1(T1), .T2(T2), .IR_LOAD(IR_BUS_IR_LOAD[0]), .IR_BUS(IR_BUS_IR_LOAD[1]));
  mem_control M (
    .M_BUS(M_BUS_M_LOAD[1]), .T1(T1), .T3(T3), .D0(D0), .D1(D1), .D2(D2), .D3(D3), .D5(D5), .D6(D6),
    .M_LOAD(M_BUS_M_LOAD[0]));
  AR ar_1 (
    .T0(T0), .T2(T2), .T3(T3), .T4(T4), .D4(D4), .D5(D5), .AR_LOAD(AR_BUS_AR_INC_AR_LOAD[0]),
    .AR_INC(AR_BUS_AR_INC_AR_LOAD[1]), .AR_BUS(AR_BUS_AR_INC_AR_LOAD[2]));
  PC pc_1 (
    .T0(T0), .T1(T1), .T3(T3), .T4(T4), .D4(D4), .D5(D5), .D6(D6), .PC_LOAD(PC_BUS_PC_INC_PC_LOAD[0]),
    .PC_INC(PC_BUS_PC_INC_PC_LOAD[1]), .PC_BUS(PC_BUS_PC_INC_PC_LOAD[2]));
  DR dr_1 (.T3(T3), .D0(D0), .D1(D1), .D2(D2), .DR_LOAD(DR_LOAD));
  E_kontrol E (
    .T3(T3), .T4(T4), .D1(D1), .D8(D8), .D11(D11), .D12(D12), .E_LOAD(E_BUS_E_CLEAR_E_LOAD[0]),
    .E_CLEAR(E_BUS_E_CLEAR_E_LOAD[1]), .E_BUS(E_BUS_E_CLEAR_E_LOAD[2]));
  AC ac_1 (
    .T3(T3), .T4(T4), .D0(D0), .D1(D1), .D2(D2), .D3(D3), .D7(D7), .D9(D9), .D10(D10), .D11(D11), .D12(D12),
    .D13(D13), .D14(D14), .AC_LOAD(AC_BUS_AC_CLEAR_AC_INC_AC_LOAD[0]),
    .AC_INC(AC_BUS_AC_CLEAR_AC_INC_AC_LOAD[1]), .AC_CLEAR(AC_BUS_AC_CLEAR_AC_INC_AC_LOAD[2]),
    .AC_BUS(AC_BUS_AC_CLEAR_AC_INC_AC_LOAD[3]));
endmodule

module sequence_counter (
  input  CLOCK,
  input  SC_CLEAR,
  output [3:0] OUTPUT
);

  wire and_1_out, register_1_q;

  Counter #(.max('hf), .width(4)) counter_1 (
    .count(1'b1), .Q(OUTPUT), .clk(CLOCK), .clr(register_1_q));  // open: load, D, carry, up
  Register #(.width(1)) register_1 (.D(SC_CLEAR), .Q(register_1_q), .clk(CLOCK), .clr(and_1_out));  // open: en
  and and_1 (and_1_out, CLOCK, SC_CLEAR);
endmodule

module sc_clear (
  input  T3,
  input  T4,
  input  D0,
  input  D1,
  input  D2,
  input  D3,
  input  D4,
  input  D5,
  input  D6,
  input  D7,
  input  D8,
  input  D9,
  input  D10,
  input  D11,
  input  D12,
  input  D13,
  input  D14,
  output out_18
);

  wire and_1_out, and_2_out, or_1_out, or_2_out;

  or or_1 (or_1_out, D0, D1, D2, D5);
  or or_2 (or_2_out, D14, D13, D12, D11, D10, D9, D8, D7, D6, D4, D3);
  and and_1 (and_1_out, or_2_out, T3);
  and and_2 (and_2_out, or_1_out, T4);
  or or_3 (out_18, and_1_out, and_2_out);
endmodule

// reg
module register_4bit (
  input  INC,
  input  LD,
  input  [3:0] L_nput,
  input  CLK,
  input  CLR,
  output [3:0] \output 
);

  wire and_1_out, and_2_out, and_3_out, and_4_out, and_5_out, and_6_out, and_7_out, and_8_out, and_9_out,
       and_10_out, and_11_out, and_12_out, not_1_out, not_2_out, not_3_out, not_4_out, not_5_out, not_6_out,
       or_1_out, or_2_out, or_3_out, or_4_out, or_5_out, or_6_out, or_7_out, or_8_out;

  not not_1 (not_1_out, LD);
  and and_1 (and_1_out, INC, not_1_out);
  not not_2 (not_2_out, not_1_out);
  not not_3 (not_3_out, L_nput[0]);
  not not_4 (not_4_out, L_nput[1]);
  not not_5 (not_5_out, L_nput[2]);
  not not_6 (not_6_out, L_nput[3]);
  and and_2 (and_2_out, not_2_out, L_nput[0]);
  and and_3 (and_3_out, not_2_out, not_3_out);
  and and_4 (and_4_out, not_2_out, L_nput[1]);
  and and_5 (and_5_out, not_2_out, not_4_out);
  and and_6 (and_6_out, not_2_out, L_nput[2]);
  and and_7 (and_7_out, not_2_out, not_5_out);
  and and_8 (and_8_out, not_2_out, L_nput[3]);
  and and_9 (and_9_out, not_2_out, not_6_out);
  and and_10 (and_10_out, and_1_out, \output [0]);
  and and_11 (and_11_out, and_1_out, \output [0], CLR);
  and and_12 (and_12_out, CLR, CLR, \output [0], and_1_out);
  or or_1 (or_1_out, and_2_out, and_1_out);
  or or_2 (or_2_out, and_3_out, and_1_out);
  or or_3 (or_3_out, and_4_out, and_10_out);
  or or_4 (or_4_out, and_10_out, and_5_out);
  or or_5 (or_5_out, and_6_out, and_11_out);
  or or_6 (or_6_out, and_11_out, and_7_out);
  or or_7 (or_7_out, and_8_out, and_12_out);
  or or_8 (or_8_out, and_12_out, and_9_out);
  J_K_Flip_Flop j_k_ff_1 (.K(CLR), .preset(\output [0]), .reset(CLR));  // open: J, clk, Q, Qn
  J_K_Flip_Flop j_k_ff_2 (.K(CLR), .clk(CLR), .Qn(\output [0]), .preset(CLR), .reset(CLR));  // open: J, Q
  J_K_Flip_Flop j_k_ff_3 (.K(CLR), .clk(CLR), .preset(CLR), .reset(CLR));  // open: J, Q, Qn
  J_K_Flip_Flop j_k_ff_4 (.K(CLR), .preset(CLR), .reset(CLR));  // open: J, clk, Q, Qn

  assign \output [3:1] = {3{CLR}};
endmodule

module instruction_register (
  input  [7:0] L_NPUT,
  input  CLK,
  input  LD,
  output [3:0] IR_0_3,
  output [3:0] IR_4_7
);

  register_4bit register_4bit_1 (.L_nput(L_NPUT[3:0]), .CLK(CLK), .LD(LD), .\output (IR_0_3));  // open: INC, CLR
  register_4bit register_4bit_2 (.L_nput(L_NPUT[7:4]), .CLK(CLK), .LD(LD), .\output (IR_4_7));  // open: INC, CLR
endmodule

module alu_1bit (
  input  INPR,
  input  DR,
  input  AC,
  input  AND,
  input  Cin,
  input  ADD,
  input  CMA,
  input  LD_DR,
  input  LD_INPR,
  input  CIR,
  input  CIL,
  input  AC_1,
  input  AC_1_2,
  output Cout,
  output AC_OUTPUT
);

  wire adder_1_out, and_1_out, and_2_out, and_3_out, LD_DR_out, LD_INPR_out, not_1_out, SHL_out, SHR_out;

  Adder #(.width(1)) adder_1 (.a(AC), .b(DR), .out(adder_1_out), .cin(Cin), .cout(Cout));
  not not_1 (not_1_out, AC);
  and and_1 (and_1_out, AND, AC, DR);
  and and_2 (and_2_out, ADD, adder_1_out);
  and and_3 (and_3_out, CMA, not_1_out);
  and u_LD_DR (LD_DR_out, LD_DR, DR);
  and u_LD_INPR (LD_INPR_out, LD_INPR, INPR);
  and SHR (SHR_out, CIR, AC_1_2);
  and SHL (SHL_out, CIL, AC_1);
  or or_1 (AC_OUTPUT, and_1_out, and_2_out, and_3_out, LD_DR_out, LD_INPR_out, SHR_out, SHL_out);
endmodule

module alu_4bit (
  input  Cin,
  input  [3:0] AC,
  input  E_AC_1_0,
  input  [3:0] DR,
  input  [3:0] INPR,
  input  AND,
  input  ADD,
  input  CMA,
  input  LD_DR,
  input  LD_INPR,
  input  CIR,
  input  CIL,
  input  E_AC_1_3,
  output [3:0] AC_OUTPUT,
  output Cout
);

  wire alu_1bit_1_cout, alu_1bit_2_cout, alu_1bit_3_cout;

  alu_1bit alu_1bit_1 (
    .AC(AC[0]), .Cin(Cin), .ADD(ADD), .CMA(CMA), .LD_DR(LD_DR), .LD_INPR(LD_INPR), .CIR(CIR), .CIL(CIL),
    .AND(AND), .AC_1(E_AC_1_0), .AC_1_2(AC[1]), .INPR(INPR[0]), .DR(DR[0]), .Cout(alu_1bit_1_cout),
    .AC_OUTPUT(AC_OUTPUT[0]));
  alu_1bit alu_1bit_2 (
    .AC(AC[1]), .Cin(alu_1bit_1_cout), .ADD(ADD), .CMA(CMA), .LD_DR(LD_DR), .LD_INPR(LD_INPR), .CIR(CIR),
    .CIL(CIL), .AND(AND), .AC_1(AC[0]), .AC_1_2(AC[2]), .INPR(INPR[1]), .DR(DR[1]), .Cout(alu_1bit_2_cout),
    .AC_OUTPUT(AC_OUTPUT[1]));
  alu_1bit alu_1bit_3 (
    .AC(AC[2]), .Cin(alu_1bit_2_cout), .ADD(ADD), .CMA(CMA), .LD_DR(LD_DR), .LD_INPR(LD_INPR), .CIR(CIR),
    .CIL(CIL), .AND(AND), .AC_1(AC[1]), .AC_1_2(AC[3]), .INPR(INPR[2]), .DR(DR[2]), .Cout(alu_1bit_3_cout),
    .AC_OUTPUT(AC_OUTPUT[2]));
  alu_1bit alu_1bit_4 (
    .AC(AC[3]), .Cin(alu_1bit_3_cout), .ADD(ADD), .CMA(CMA), .LD_DR(LD_DR), .LD_INPR(LD_INPR), .CIR(CIR),
    .CIL(CIL), .AND(AND), .AC_1(AC[2]), .AC_1_2(E_AC_1_3), .INPR(INPR[3]), .DR(DR[3]), .Cout(Cout),
    .AC_OUTPUT(AC_OUTPUT[3]));

  // Notes on the sheet:
  //   AC(0)
endmodule

module E (
  input  Cin,
  input  ADD,
  input  in_3,
  input  CIR,
  input  AC_1,
  input  CIL,
  input  CLK,
  output OUTPUT,
  output out_9,
  output AC_1_2,
  output out_11
);

  wire and_1_out, and_2_out, and_3_out, and_4_out, and_5_out, d_ff_1_p3, not_1_out, or_1_out, or_2_out;

  and and_1 (and_1_out, Cin, ADD);
  and and_2 (and_2_out, in_3, CIR);
  or or_1 (or_1_out, and_1_out, and_2_out, and_3_out);
  and and_3 (and_3_out, AC_1, CIL);
  not not_1 (not_1_out, or_1_out);
  or or_2 (or_2_out, in_3, Cin, AC_1);
  and and_4 (and_4_out, or_2_out, or_1_out);
  and and_5 (and_5_out, not_1_out, or_2_out);
  S_R_Flip_Flop s_r_ff_1 (.S(and_4_out), .clk(CLK), .R(and_5_out), .Q(OUTPUT));  // open: Qn, preset, reset
  // D_Flip_Flop d_ff_1: pin names not known; wires that end beside it: CLK, OUTPUT, d_ff_1_p3
  and and_6 (out_9, d_ff_1_p3, and_1_out);
  and and_7 (AC_1_2, d_ff_1_p3, and_2_out);
  and and_8 (out_11, d_ff_1_p3, and_3_out);
endmodule

module alu_4bit_carry (
  input  [3:0] AC,
  input  [3:0] DR,
  input  [3:0] INPR,
  input  AND,
  input  ADD,
  input  CMA,
  input  LD_DR,
  input  LD_INPR,
  input  CIR,
  input  CIL,
  input  CLK,
  output [3:0] AC_OUTPUT,
  output Cout
);

  wire alu_1bit_1_cout, alu_1bit_2_cout, alu_1bit_3_cout, alu_1bit_4_cout, e_1_ac_1_2, e_1_out_9, e_1_out_11;

  alu_1bit alu_1bit_1 (
    .AC(AC[0]), .Cin(e_1_out_9), .ADD(ADD), .CMA(CMA), .LD_DR(LD_DR), .LD_INPR(LD_INPR), .CIR(CIR),
    .CIL(CIL), .AND(AND), .AC_1(e_1_ac_1_2), .AC_1_2(AC[1]), .INPR(INPR[0]), .DR(DR[0]),
    .Cout(alu_1bit_1_cout), .AC_OUTPUT(AC_OUTPUT[0]));
  alu_1bit alu_1bit_2 (
    .AC(AC[1]), .Cin(alu_1bit_1_cout), .ADD(ADD), .CMA(CMA), .LD_DR(LD_DR), .LD_INPR(LD_INPR), .CIR(CIR),
    .CIL(CIL), .AND(AND), .AC_1(AC[0]), .AC_1_2(AC[2]), .INPR(INPR[1]), .DR(DR[1]), .Cout(alu_1bit_2_cout),
    .AC_OUTPUT(AC_OUTPUT[1]));
  alu_1bit alu_1bit_3 (
    .AC(AC[2]), .Cin(alu_1bit_2_cout), .ADD(ADD), .CMA(CMA), .LD_DR(LD_DR), .LD_INPR(LD_INPR), .CIR(CIR),
    .CIL(CIL), .AND(AND), .AC_1(AC[1]), .AC_1_2(AC[3]), .INPR(INPR[2]), .DR(DR[2]), .Cout(alu_1bit_3_cout),
    .AC_OUTPUT(AC_OUTPUT[2]));
  alu_1bit alu_1bit_4 (
    .AC(AC[3]), .Cin(alu_1bit_3_cout), .ADD(ADD), .CMA(CMA), .LD_DR(LD_DR), .LD_INPR(LD_INPR), .CIR(CIR),
    .CIL(CIL), .AND(AND), .AC_1(AC[2]), .AC_1_2(e_1_out_11), .INPR(INPR[3]), .DR(DR[3]),
    .Cout(alu_1bit_4_cout), .AC_OUTPUT(AC_OUTPUT[3]));
  E e_1 (
    .Cin(alu_1bit_4_cout), .ADD(ADD), .in_3(e_1_out_11), .CIR(CIR), .AC_1(e_1_ac_1_2), .CIL(CIL), .CLK(CLK),
    .OUTPUT(Cout), .out_9(e_1_out_9), .AC_1_2(e_1_ac_1_2), .out_11(e_1_out_11));

  // Notes on the sheet:
  //   AC(0)
endmodule

module AR (
  input  T0,
  input  T2,
  input  T3,
  input  T4,
  input  D4,
  input  D5,
  output AR_LOAD,
  output AR_INC,
  output AR_BUS
);

  wire and_2_out, and_3_out;

  or or_1 (AR_LOAD, T0, T2);
  and and_1 (AR_INC, D5, T3);
  and and_2 (and_2_out, D4, T3);
  or or_2 (AR_BUS, and_2_out, and_3_out);
  and and_3 (and_3_out, D5, T4);
endmodule

module PC (
  input  T0,
  input  T1,
  input  T3,
  input  T4,
  input  D4,
  input  D5,
  input  D6,
  output PC_LOAD,
  output PC_INC,
  output PC_BUS
);

  wire and_1_out, and_2_out, and_3_out, or_1_out;

  or or_1 (or_1_out, D4, D6);
  and and_1 (and_1_out, or_1_out, T3);
  and and_2 (and_2_out, D4, D5);
  and and_3 (and_3_out, T3, D5);
  or or_2 (PC_LOAD, and_1_out, and_2_out);
  or or_3 (PC_BUS, and_3_out, T0);

  assign PC_INC = T1;
endmodule

module mem_control (
  input  T1,
  input  T3,
  input  D0,
  input  D1,
  input  D2,
  input  D3,
  input  D5,
  input  D6,
  output M_LOAD,
  output M_BUS
);

  wire and_1_out, or_1_out, or_2_out;

  or or_1 (or_1_out, D5, D3);
  or or_2 (or_2_out, D0, D1, D2, D6);
  and and_1 (and_1_out, or_2_out, T3);
  and and_2 (M_LOAD, or_1_out, T3);
  or or_3 (M_BUS, and_1_out, T1);
endmodule

module DR (
  input  T3,
  input  D0,
  input  D1,
  input  D2,
  output DR_LOAD
);

  wire or_1_out;

  or or_1 (or_1_out, D2, D1, D0);
  and and_1 (DR_LOAD, or_1_out, T3);
endmodule

module OUTR (
  input  T3,
  input  D14,
  output OUTR_LOAD
);

  and and_1 (OUTR_LOAD, D14, T3);
endmodule

module IR (
  input  T1,
  input  T2,
  output IR_LOAD,
  output IR_BUS
);


  assign IR_BUS = T2;
  assign IR_LOAD = T1;
endmodule

module AC (
  input  T3,
  input  T4,
  input  D0,
  input  D1,
  input  D2,
  input  D3,
  input  D7,
  input  D9,
  input  D10,
  input  D11,
  input  D12,
  input  D13,
  input  D14,
  output AC_LOAD,
  output AC_INC,
  output AC_CLEAR,
  output AC_BUS
);

  wire and_1_out, and_2_out, or_1_out, or_2_out, or_3_out;

  or or_1 (or_1_out, D0, D2, D1);
  or or_2 (or_2_out, D9, D11, D12, D13);
  or or_3 (or_3_out, D14, D3);
  and and_1 (and_1_out, or_1_out, T4);
  and and_2 (and_2_out, T3, or_2_out);
  or or_4 (AC_LOAD, and_1_out, and_2_out);
  and and_3 (AC_INC, T3, D10);
  and and_4 (AC_CLEAR, D7, T3);
  and and_5 (AC_BUS, or_3_out, T3);
endmodule

module ALU (
  input  T3,
  input  T4,
  input  D0,
  input  D1,
  input  D2,
  input  D9,
  input  D11,
  input  D12,
  input  D13,
  output AND,
  output ADD,
  output CMA,
  output DR_LOAD,
  output LD_INPR,
  output CIR,
  output CIL
);

  and and_1 (AND, D0, T4);
  and and_2 (ADD, D1, T4);
  and and_3 (CMA, D9, T3);
  and and_4 (DR_LOAD, D2, T4);
  and and_5 (LD_INPR, D13, T3);
  and and_6 (CIR, D11, T3);
  and and_7 (CIL, D12, T3);
endmodule

module E_kontrol (
  input  T3,
  input  T4,
  input  D1,
  input  D8,
  input  D11,
  input  D12,
  output E_LOAD,
  output E_CLEAR,
  output E_BUS
);

  wire and_1_out, and_2_out, or_1_out, or_2_out;

  or or_1 (or_1_out, D12, D11);
  and and_1 (and_1_out, D1, T4);
  and and_2 (and_2_out, or_1_out, T3);
  or or_2 (or_2_out, D12, D11);
  or or_3 (E_LOAD, and_1_out, and_2_out);
  and and_3 (E_CLEAR, D8, T3);
  and and_4 (E_BUS, or_2_out, T3);
endmodule
